// Digital circuit 4x4_carry_save_multiplier.dig as structural Verilog
module _4x4_carry_save_multiplier (
  input  [3:0] in_1,
  input  [3:0] in_2,
  output [7:0] out_3
);

  wire add_2_c_o, add_2_s, add_3_c_o, add_4_c_o, add_4_s, add_5_c_o, add_5_s, add_6_c_o, add_6_s, add_7_c_o,
       add_7_s, add_8_c_o, add_9_c_o, add_9_s, add_10_c_o, add_10_s, add_11_c_o, add_12_c_o, add_12_s,
       add_13_c_o, add_14_c_o, add_14_s, add_15_c_o, add_16_c_o;
  wire [3:0] multiplexer_2_out, multiplexer_3_out, multiplexer_4_out;
  wire [3:1] multiplexer_1_out;

  Add add_1 (.a(add_3_c_o), .b(add_2_c_o), .c_i(1'b0), .s(out_3[7]));  // open: c_o
  Add add_2 (.a(add_4_c_o), .b(multiplexer_4_out[3]), .c_i(1'b0), .s(add_2_s), .c_o(add_2_c_o));
  Add add_3 (.a(add_8_c_o), .b(add_5_c_o), .c_i(add_2_s), .s(out_3[6]), .c_o(add_3_c_o));
  Add add_4 (.a(add_6_c_o), .b(multiplexer_3_out[3]), .c_i(1'b0), .s(add_4_s), .c_o(add_4_c_o));
  Add add_5 (.a(add_7_c_o), .b(multiplexer_4_out[2]), .c_i(add_4_s), .s(add_5_s), .c_o(add_5_c_o));
  Add add_6 (.a(1'b0), .b(multiplexer_2_out[3]), .c_i(1'b0), .s(add_6_s), .c_o(add_6_c_o));
  Add add_7 (.a(add_9_c_o), .b(multiplexer_3_out[2]), .c_i(add_6_s), .s(add_7_s), .c_o(add_7_c_o));
  Add add_8 (.a(add_11_c_o), .b(add_10_c_o), .c_i(add_5_s), .s(out_3[5]), .c_o(add_8_c_o));
  Add add_9 (.a(multiplexer_1_out[3]), .b(multiplexer_2_out[2]), .c_i(1'b0), .s(add_9_s), .c_o(add_9_c_o));
  Add add_10 (.a(add_12_c_o), .b(multiplexer_4_out[1]), .c_i(add_7_s), .s(add_10_s), .c_o(add_10_c_o));
  Add add_11 (.a(1'b0), .b(add_13_c_o), .c_i(add_10_s), .s(out_3[4]), .c_o(add_11_c_o));
  Add add_12 (.a(add_14_c_o), .b(multiplexer_3_out[1]), .c_i(add_9_s), .s(add_12_s), .c_o(add_12_c_o));
  Add add_13 (.a(add_15_c_o), .b(multiplexer_4_out[0]), .c_i(add_12_s), .s(out_3[3]), .c_o(add_13_c_o));
  Add add_14 (.a(multiplexer_1_out[2]), .b(multiplexer_2_out[1]), .c_i(1'b0), .s(add_14_s), .c_o(add_14_c_o));
  Add add_15 (.a(add_16_c_o), .b(multiplexer_3_out[0]), .c_i(add_14_s), .s(out_3[2]), .c_o(add_15_c_o));
  Add add_16 (.a(multiplexer_1_out[1]), .b(multiplexer_2_out[0]), .c_i(1'b0), .s(out_3[1]), .c_o(add_16_c_o));
  Multiplexer #(.Bits(4)) multiplexer_1 (
    .sel(in_2[0]), .in_0(4'b0000), .in_1(in_1), .out({multiplexer_1_out, out_3[0]}));
  Multiplexer #(.Bits(4)) multiplexer_2 (.sel(in_2[1]), .in_0(4'b0000), .in_1(in_1), .out(multiplexer_2_out));
  Multiplexer #(.Bits(4)) multiplexer_3 (.sel(in_2[2]), .in_0(4'b0000), .in_1(in_1), .out(multiplexer_3_out));
  Multiplexer #(.Bits(4)) multiplexer_4 (.sel(in_2[3]), .in_0(4'b0000), .in_1(in_1), .out(multiplexer_4_out));
endmodule
