// Digital circuit bitwise_full_adder.dig as structural Verilog
module bitwise_full_adder (
  input  [7:0] X,
  input  [7:0] Y,
  input  [7:0] Z,
  output [7:0] S,
  output [7:0] C
);

  Add add_1 (.a(X[0]), .b(Y[0]), .c_i(Z[0]), .s(S[0]), .c_o(C[0]));
  Add add_2 (.a(X[1]), .b(Y[1]), .c_i(Z[1]), .s(S[1]), .c_o(C[1]));
  Add add_3 (.a(X[2]), .b(Y[2]), .c_i(Z[2]), .s(S[2]), .c_o(C[2]));
  Add add_4 (.a(X[3]), .b(Y[3]), .c_i(Z[3]), .s(S[3]), .c_o(C[3]));
  Add add_5 (.a(X[4]), .b(Y[4]), .c_i(Z[4]), .s(S[4]), .c_o(C[4]));
  Add add_6 (.a(X[5]), .b(Y[5]), .c_i(Z[5]), .s(S[5]), .c_o(C[5]));
  Add add_7 (.a(X[6]), .b(Y[6]), .c_i(Z[6]), .s(S[6]), .c_o(C[6]));
  Add add_8 (.a(X[7]), .b(Y[7]), .c_i(Z[7]), .s(S[7]), .c_o(C[7]));
endmodule
