// Digital circuit carry_op.dig as structural Verilog
module carry_op (
  input  [1:0] G__P,
  input  [1:0] G__P_2,
  output [1:0] G_P
);

  wire and_1_out;

  or or_1 (G_P[1], and_1_out, G__P[1]);
  and and_1 (and_1_out, G__P_2[1], G__P[0]);
  and and_2 (G_P[0], G__P_2[0], G__P[0]);
endmodule
