// Digital circuit carry_save_adder.dig as structural Verilog
module carry_save_adder (
  input  [15:0] X,
  input  [15:0] Y,
  input  [15:0] Z,
  output [15:0] S,
  output [15:0] C
);

  wire [7:0] bitwise_full_adder_1_c, bitwise_full_adder_2_c;

  bitwise_full_adder bitwise_full_adder_1 (.X(X[7:0]), .Y(Y[7:0]), .Z(Z[7:0]), .S(S[7:0]), .C(bitwise_full_adder_1_c));
  bitwise_full_adder bitwise_full_adder_2 (
    .X(X[15:8]), .Y(Y[15:8]), .Z(Z[15:8]), .S(S[15:8]), .C(bitwise_full_adder_2_c));
  BarrelShifter #(.Bits(16)) barrelshifter_1 (
    .in({bitwise_full_adder_2_c, bitwise_full_adder_1_c}), .shift(5'b00001), .out(C));
endmodule
