// Digital circuit carry_save_multiplier.dig as structural Verilog
module carry_save_multiplier (
  input  [15:0] x0,
  input  [15:0] x1,
  input  [15:0] x2,
  input  [15:0] x3,
  input  [15:0] x4,
  input  [15:0] x5,
  input  [15:0] x6,
  input  [15:0] x7,
  output [15:0] out_9
);

  wire [15:0] carry_save_adder_1_c, carry_save_adder_1_s, carry_save_adder_2_c, carry_save_adder_2_s,
       carry_save_adder_3_c, carry_save_adder_3_s, carry_save_adder_4_c, carry_save_adder_4_s,
       carry_save_adder_5_c, carry_save_adder_5_s, carry_save_adder_6_c, carry_save_adder_6_s;

  carry_save_adder carry_save_adder_1 (.X(x0), .Y(x1), .Z(x2), .S(carry_save_adder_1_s), .C(carry_save_adder_1_c));
  carry_save_adder carry_save_adder_2 (.X(x3), .Y(x4), .Z(x5), .S(carry_save_adder_2_s), .C(carry_save_adder_2_c));
  carry_save_adder carry_save_adder_3 (
    .X(carry_save_adder_1_s), .Y(carry_save_adder_1_c), .Z(carry_save_adder_2_s), .S(carry_save_adder_3_s),
    .C(carry_save_adder_3_c));
  carry_save_adder carry_save_adder_4 (
    .X(carry_save_adder_2_c), .Y(x6), .Z(x7), .S(carry_save_adder_4_s), .C(carry_save_adder_4_c));
  carry_save_adder carry_save_adder_5 (
    .X(carry_save_adder_3_s), .Y(carry_save_adder_3_c), .Z(carry_save_adder_4_s), .S(carry_save_adder_5_s),
    .C(carry_save_adder_5_c));
  carry_save_adder carry_save_adder_6 (
    .X(carry_save_adder_5_s), .Y(carry_save_adder_5_c), .Z(carry_save_adder_4_c), .S(carry_save_adder_6_s),
    .C(carry_save_adder_6_c));
  Add #(.Bits(16)) add_1 (.a(carry_save_adder_6_s), .b(carry_save_adder_6_c), .c_i(1'b0), .s(out_9));  // open: c_o
endmodule
