// Digital circuit dil_test.dig as structural Verilog
module dil_test (
  input  A,
  input  B,
  output C
);

  and and_1 (C, A, B);

  // Notes on the sheet:
  //   B: pin 1
  //   C: pin 5
endmodule
