// Digital circuit input_half_adder.dig as structural Verilog
module input_half_adder (
  input  A,
  input  B,
  output [1:0] G_P,
  output H
);

  xor xor_1 (H, B, A);
  and and_1 (G_P[1], B, A);
  or or_1 (G_P[0], B, A);
endmodule
