// Digital circuit ladner-fischer.dig as structural Verilog
module ladner_fischer (
  input  A3,
  input  B3,
  input  A2,
  input  B2,
  input  A1,
  input  B1,
  input  A0,
  input  B0,
  output S1,
  output S0,
  output S2,
  output S3,
  output S4
);

  wire HA_2_h, HA_3_h, HA_h;
  wire [0:0] carry_op_2_g_p;
  wire [1:0] carry_op_3_g_p, carry_op_4_g_p, carry_op_g_p, HA_2_g_p, HA_3_g_p, HA_4_g_p, HA_g_p;

  input_half_adder HA (.A(A3), .B(B3), .H(HA_h), .G_P(HA_g_p));
  carry_op carry_op (.G__P(HA_g_p), .G__P_2(HA_2_g_p), .G_P(carry_op_g_p));
  carry_op carry_op_2 (.G__P(carry_op_g_p), .G__P_2(carry_op_4_g_p), .G_P({S4, carry_op_2_g_p[0]}));
  xor xor_1 (S3, carry_op_3_g_p[1], HA_h);
  input_half_adder HA_2 (.A(A2), .B(B2), .H(HA_2_h), .G_P(HA_2_g_p));
  carry_op carry_op_3 (.G__P(HA_2_g_p), .G__P_2(carry_op_4_g_p), .G_P(carry_op_3_g_p));
  xor xor_2 (S2, carry_op_4_g_p[1], HA_2_h);
  input_half_adder HA_3 (.A(A1), .B(B1), .H(HA_3_h), .G_P(HA_3_g_p));
  carry_op carry_op_4 (.G__P(HA_3_g_p), .G__P_2(HA_4_g_p), .G_P(carry_op_4_g_p));
  xor xor_3 (S1, HA_4_g_p[1], HA_3_h);
  input_half_adder HA_4 (.A(A0), .B(B0), .H(S0), .G_P(HA_4_g_p));
endmodule
