// Digital circuit plus3.dig as structural Verilog
module plus3 (
  input  [3:0] in,
  output [3:0] out
);

  wire comparator_1_gt;
  wire [3:0] add_1_s;

  Comparator #(.Bits(4)) comparator_1 (.a(in), .b(4'b0100), .gt(comparator_1_gt));  // open: eq, lt
  Add #(.Bits(4)) add_1 (.a(4'b0011), .b(in), .c_i(1'b0), .s(add_1_s));  // open: c_o
  Multiplexer #(.Bits(4)) multiplexer_1 (.sel(comparator_1_gt), .in_0(in), .in_1(add_1_s), .out(out));
endmodule
