// Digital circuit plus3_mux.dig as structural Verilog
module plus3_mux (
  input  [3:0] in,
  output [3:0] out
);

  wire and_2_out, or_1_out, or_2_out;
  wire [2:0] not_1_out;

  xnor xnor_1 (not_1_out[1], in[0], in[1]);
  or or_1 (or_1_out, in[0], in[1]);
  not not_1 (not_1_out[0], in[0]);
  and and_1 (not_1_out[2], in[0], in[3]);
  and and_2 (and_2_out, or_1_out, in[2]);
  or or_2 (or_2_out, and_2_out, in[3]);
  Multiplexer #(.Bits(4)) multiplexer_1 (.sel(or_2_out), .in_0(in), .in_1({1'b1, not_1_out}), .out(out));

  // Notes on the sheet:
  //   check in>4
  //   in
  //   in+3
endmodule

/* Test case:
in out
0 0
1 1
2 2
3 3
4 4
5 8
6 9
7 10
8 11
9 12
*/
