// Logisim project 4 bit lfsr.circ as structural Verilog: 1 circuit, main circuit main
module main (
);

  wire clock_1_out, pull_resistor_1_node;
  wire [3:0] shift_register_1_q3;

  Clock clock_1 (.out(clock_1_out));
  Shift_Register #(.length(4)) shift_register_1 (
    .in(pull_resistor_1_node), .clk(clock_1_out), .q0(shift_register_1_q3[3]), .q1(shift_register_1_q3[2]),
    .q2(shift_register_1_q3[1]), .q3(shift_register_1_q3[0]));  // open: shift, out, load, clr, d0, d1, d2, d3
  Pull_Resistor pull_resistor_1 (.node(pull_resistor_1_node));
  xor xor_1 (pull_resistor_1_node, shift_register_1_q3[1], shift_register_1_q3[0]);
  Hex_Digit_Display hex_digit_display_1 (.value(shift_register_1_q3));  // open: dp
endmodule
