// Logisim project 8 bit binary to bcd.circ as structural Verilog: 2 circuits, main circuit main
module main (
  input  _1,
  input  _2,
  input  _4,
  input  _8,
  input  _16,
  input  _32,
  input  _64,
  input  _128
);

  wire bcd_unit_1_out_5, bcd_unit_1_out_6, bcd_unit_1_out_7, bcd_unit_1_out_8, bcd_unit_2_out_5,
       bcd_unit_2_out_6, bcd_unit_2_out_7, bcd_unit_2_out_8, bcd_unit_3_out_5, bcd_unit_3_out_6,
       bcd_unit_3_out_7, bcd_unit_3_out_8, bcd_unit_4_out_5, bcd_unit_4_out_6, bcd_unit_4_out_7,
       bcd_unit_4_out_8, bcd_unit_5_out_5, bcd_unit_5_out_6, bcd_unit_5_out_7;
  wire [1:0] bcd_unit_7_out_8;
  wire [3:0] bcd_unit_6_out_8;
  wire [3:1] bcd_unit_6_out_5;

  BCD_Unit bcd_unit_1 (
    .in_1(_16), .in_2(bcd_unit_2_out_5), .in_3(bcd_unit_2_out_6), .in_4(bcd_unit_2_out_7),
    .out_5(bcd_unit_1_out_5), .out_6(bcd_unit_1_out_6), .out_7(bcd_unit_1_out_7), .out_8(bcd_unit_1_out_8));
  BCD_Unit bcd_unit_2 (
    .in_1(_32), .in_2(_64), .in_3(_128), .in_4(1'b0), .out_5(bcd_unit_2_out_5), .out_6(bcd_unit_2_out_6),
    .out_7(bcd_unit_2_out_7), .out_8(bcd_unit_2_out_8));
  BCD_Unit bcd_unit_3 (
    .in_1(_8), .in_2(bcd_unit_1_out_5), .in_3(bcd_unit_1_out_6), .in_4(bcd_unit_1_out_7),
    .out_5(bcd_unit_3_out_5), .out_6(bcd_unit_3_out_6), .out_7(bcd_unit_3_out_7), .out_8(bcd_unit_3_out_8));
  BCD_Unit bcd_unit_4 (
    .in_1(_4), .in_2(bcd_unit_3_out_5), .in_3(bcd_unit_3_out_6), .in_4(bcd_unit_3_out_7),
    .out_5(bcd_unit_4_out_5), .out_6(bcd_unit_4_out_6), .out_7(bcd_unit_4_out_7), .out_8(bcd_unit_4_out_8));
  BCD_Unit bcd_unit_5 (
    .in_1(bcd_unit_3_out_8), .in_2(bcd_unit_1_out_8), .in_3(bcd_unit_2_out_8), .in_4(1'b0),
    .out_5(bcd_unit_5_out_5), .out_6(bcd_unit_5_out_6), .out_7(bcd_unit_5_out_7), .out_8(bcd_unit_7_out_8[1]));
  BCD_Unit bcd_unit_6 (
    .in_1(_2), .in_2(bcd_unit_4_out_5), .in_3(bcd_unit_4_out_6), .in_4(bcd_unit_4_out_7),
    .out_5(bcd_unit_6_out_5[1]), .out_6(bcd_unit_6_out_5[2]), .out_7(bcd_unit_6_out_5[3]),
    .out_8(bcd_unit_6_out_8[0]));
  BCD_Unit bcd_unit_7 (
    .in_1(bcd_unit_4_out_8), .in_2(bcd_unit_5_out_5), .in_3(bcd_unit_5_out_6), .in_4(bcd_unit_5_out_7),
    .out_5(bcd_unit_6_out_8[1]), .out_6(bcd_unit_6_out_8[2]), .out_7(bcd_unit_6_out_8[3]),
    .out_8(bcd_unit_7_out_8[0]));
  Hex_Digit_Display hex_digit_display_1 (.value(bcd_unit_6_out_8));  // open: dp
  Hex_Digit_Display hex_digit_display_2 (.value({2'b00, bcd_unit_7_out_8}));  // open: dp
  Hex_Digit_Display hex_digit_display_3 (.value({bcd_unit_6_out_5, _1}));  // open: dp
endmodule

module BCD_Unit (
  input  in_1,
  input  in_2,
  input  in_3,
  input  in_4,
  output out_5,
  output out_6,
  output out_7,
  output out_8
);

  wire and_1_out, or_1_out, or_2_out;
  wire [3:0] adder_1_out;

  or or_1 (or_1_out, in_1, in_2);
  and and_1 (and_1_out, or_1_out, in_3);
  Adder #(.width(4)) adder_1 (.a({in_4, in_3, in_2, in_1}), .b(4'b0011), .out(adder_1_out));  // open: cin, cout
  or or_2 (or_2_out, and_1_out, in_4);
  Multiplexer #(.width(4)) multiplexer_1 (
    .in0({in_4, in_3, in_2, in_1}), .in1(adder_1_out), .out({out_8, out_7, out_6, out_5}), .sel(or_2_out));  // open: en
endmodule
