// Logisim project ALU 1.circ as structural Verilog: 2 circuits, main circuit main
module main (
  input  [7:0] in_1,
  input  [7:0] B,
  input  [1:0] Opcode,
  output out_4,
  output [7:0] out_5,
  output [7:0] out_6
);

  wire adder_1_cout, or_1_out, or_3_out_2, subtractor_1_bout, undriven;
  wire [7:0] adder_1_out, demultiplexer_1_out0, demultiplexer_1_out1, demultiplexer_1_out2,
       demultiplexer_1_out3, demultiplexer_2_out0, demultiplexer_2_out1, demultiplexer_2_out2,
       demultiplexer_2_out3, divider_1_out, multiplier_1_out, subtractor_1_out;

  Demultiplexer #(.select(2), .width(8)) demultiplexer_1 (
    .out0(demultiplexer_1_out0), .out1(demultiplexer_1_out1), .out2(demultiplexer_1_out2),
    .out3(demultiplexer_1_out3), .in(B), .sel(Opcode));  // open: en
  Demultiplexer #(.select(2), .width(8)) demultiplexer_2 (
    .out0(demultiplexer_2_out0), .out1(demultiplexer_2_out1), .out2(demultiplexer_2_out2),
    .out3(demultiplexer_2_out3), .in(in_1), .sel(Opcode), .en(undriven));
  or or_1 (or_1_out, out_4, or_3_out_2);
  LED led_1 (.in(or_1_out));
  Adder adder_1 (
    .a(demultiplexer_2_out0), .b(demultiplexer_1_out0), .out(adder_1_out), .cout(adder_1_cout));  // open: cin
  or or_2 (out_4, adder_1_cout, subtractor_1_bout);
  Subtractor subtractor_1 (
    .a(demultiplexer_2_out1), .b(demultiplexer_1_out1), .out(subtractor_1_out), .bout(subtractor_1_bout));  // open: bin
  \or  or_3 (.in_1(out_6), .out_2(or_3_out_2));
  Multiplier multiplier_1 (
    .a(demultiplexer_2_out2), .b(demultiplexer_1_out2), .out(multiplier_1_out), .cout(out_6));  // open: cin
  assign out_5 = adder_1_out | subtractor_1_out | multiplier_1_out | divider_1_out;  // OR_Gate or_4, 8 bits wide
  Divider divider_1 (.a(demultiplexer_2_out3), .b(demultiplexer_1_out3), .out(divider_1_out));  // open: upper, rem

  // Notes on the sheet:
  //   A
  //   Overflow
  //   Sum/subtract carry
  //   Multiplication carry
endmodule

module \or  (
  input  [7:0] in_1,
  output out_2
);

  wire or_1_out, or_2_out;

  or or_1 (or_1_out, in_1[7], in_1[6], in_1[5], in_1[4]);
  or or_2 (or_2_out, in_1[3], in_1[2], in_1[1], in_1[0]);
  or or_3 (out_2, or_1_out, or_2_out);
endmodule
