// Logisim project ANSI C Linear congruence generator.circ as structural Verilog: 1 circuit, main circuit main
module main (
);

  wire clock_1_out;
  wire [30:0] adder_1_out, multiplier_1_out, register_1_q;

  Multiplier #(.width(31)) multiplier_1 (
    .a(register_1_q), .b(31'h41c64e6d), .out(multiplier_1_out));  // open: cin, cout
  Adder #(.width(31)) adder_1 (.a(multiplier_1_out), .b(31'h3039), .out(adder_1_out));  // open: cin, cout
  Register #(.width(31)) register_1 (.D(adder_1_out), .Q(register_1_q), .clk(clock_1_out));  // open: en, clr
  Clock clock_1 (.out(clock_1_out));
  // Probe on register_1_q[30:16]
endmodule
