// Logisim project BOB.circ as structural Verilog: 11 circuits, main circuit main
module main (
  input  [4:0] in_1,
  input  in_2,
  input  [3:0] in_3,
  input  [3:0] in_4,
  input  [15:0] in_5
);

  wire and_1_out, buffer_1_out, C_out, clock_1_out, d_ff_1_q, d_ff_1_qn, E_out;
  wire [15:0] bob_1_out_5, bob_1_pcrom;
  wire [29:0] rom_1_data;

  Button E (.out(E_out));
  buf buffer_1 (buffer_1_out, E_out);
  and and_1 (and_1_out, E_out, d_ff_1_qn);
  D_Flip_Flop d_ff_1 (.clk(buffer_1_out), .D(and_1_out), .Q(d_ff_1_q), .Qn(d_ff_1_qn));  // open: preset, en, reset
  Clock clock_1 (.out(clock_1_out));
  Button C (.out(C_out));
  Hex_Digit_Display hex_digit_display_1 (.value({2'b00, in_5[15:14]}));  // open: dp
  Hex_Digit_Display hex_digit_display_2 (.value(in_5[9:6]));  // open: dp
  Hex_Digit_Display hex_digit_display_3 (.value(in_5[13:10]));  // open: dp
  ROM #(.addrWidth(16), .dataWidth(30)) rom_1 (.addr(bob_1_pcrom), .data(rom_1_data));  // open: sel
  Hex_Digit_Display hex_digit_display_4 (.value(in_5[5:2]));  // open: dp
  Hex_Digit_Display hex_digit_display_5 (.value({in_5[1:0], in_4[3:2]}));  // open: dp
  BOB bob_1 (
    .PCROM(bob_1_pcrom), .EXECUTE(d_ff_1_q), .CLK(clock_1_out), .CLR(C_out), .WORD(rom_1_data),
    .out_5(bob_1_out_5));
  Hex_Digit_Display hex_digit_display_6 (.value({in_3[1:0], in_2, in_1[4]}));  // open: dp
  Hex_Digit_Display hex_digit_display_7 (.value({in_4[1:0], in_3[3:2]}));  // open: dp
  Hex_Digit_Display hex_digit_display_8 (.value(in_1[3:0]));  // open: dp
  // Probe on bob_1_out_5
  // Probe on bob_1_out_5

  // Notes on the sheet:
  //   Press the E button to power on/off the BOB CPU.
  //   Press the C button to reset the BOB CPU
  //   WELCOME!
  //   contents of rom_1 (hex, n*v repeats v):
  //   0 4414 c015 76 874 42a b4 e
  //   To turn on the clock, press Ctrl+K
  //   To adjust the speed, go to Simulate > Tick Frequency.
  //   The current program stored in the ROM is the Fibonacci sequence.
  //   Output - Binary and decimal
  //   The BOB is only 16 bits, so the output will overflow pretty quickly ;)
endmodule

module NEGATOR (
  input  [15:0] A,
  input  in_2,
  output [15:0] Y
);

  wire [15:0] negator_1_out;

  Multiplexer #(.width(16), .enable("false")) multiplexer_1 (.in0(A), .in1(negator_1_out), .out(Y), .sel(in_2));
  Negator #(.width(16)) negator_1 (.in(A), .out(negator_1_out));
endmodule

module LOGIC (
  input  NOT_B,
  input  NOT,
  input  AND,
  input  OR,
  input  XOR,
  input  [15:0] A,
  input  [15:0] B,
  output [15:0] Y
);

  wire or_2_out;
  wire [15:0] and_1_out, multiplexer_1_out, multiplexer_2_out, multiplexer_3_out, multiplexer_4_out,
       multiplexer_5_out, not_1_out, or_1_out, xor_1_out;

  Multiplexer #(.width(16), .enable("false")) multiplexer_1 (.in0(A), .in1(B), .out(multiplexer_1_out), .sel(NOT_B));
  assign and_1_out = A & B;  // AND_Gate and_1, 16 bits wide
  assign or_1_out = A | B;  // OR_Gate or_1, 16 bits wide
  assign xor_1_out = A ^ B;  // XOR_Gate xor_1, 16 bits wide
  or or_2 (or_2_out, NOT_B, NOT);
  Multiplexer #(.width(16), .enable("false")) multiplexer_2 (
    .in0({16{1'b0}}), .in1(not_1_out), .out(multiplexer_2_out), .sel(or_2_out));
  assign not_1_out = ~multiplexer_1_out;  // NOT_Gate not_1, 16 bits wide
  Multiplexer #(.width(16), .enable("false")) multiplexer_3 (
    .in0({16{1'b0}}), .in1(and_1_out), .out(multiplexer_3_out), .sel(AND));
  Multiplexer #(.width(16), .enable("false")) multiplexer_4 (
    .in0({16{1'b0}}), .in1(or_1_out), .out(multiplexer_4_out), .sel(OR));
  Multiplexer #(.width(16), .enable("false")) multiplexer_5 (
    .in0({16{1'b0}}), .in1(xor_1_out), .out(multiplexer_5_out), .sel(XOR));
  assign Y = multiplexer_2_out | multiplexer_3_out | multiplexer_4_out | multiplexer_5_out;  // OR_Gate or_3, 16 bits wide
endmodule

module MUL_OVERFLOW_CHECK (
  input  [15:0] A,
  input  [15:0] B,
  input  [15:0] Y,
  output OVERFLOW
);

  wire comparator_1_lt;
  wire [15:0] multiplexer_1_out;

  Comparator #(.width(16)) comparator_1 (.a(A), .b(B), .lt(comparator_1_lt));  // open: gt, eq
  Comparator #(.width(16)) comparator_2 (.a(multiplexer_1_out), .b(Y), .gt(OVERFLOW));  // open: eq, lt
  Multiplexer #(.width(16), .disabled(0), .enable("false")) multiplexer_1 (
    .in0(A), .in1(B), .out(multiplexer_1_out), .sel(comparator_1_lt));
endmodule

module ARITHMETIC (
  input  ADD,
  input  SUB,
  input  MUL,
  input  DIV,
  input  [15:0] A,
  input  [15:0] B,
  output [15:0] Y,
  output Overflow
);

  wire adder_1_cout, mul_overflow_check_1_overflow, subtractor_1_bout;
  wire [15:0] adder_1_out, divider_1_out, multiplexer_1_out, multiplexer_2_out, multiplexer_3_out,
       multiplexer_4_out, multiplier_1_out, subtractor_1_out;

  Adder #(.width(16)) adder_1 (.a(A), .b(B), .out(adder_1_out), .cout(adder_1_cout));  // open: cin
  Subtractor #(.width(16)) subtractor_1 (.a(A), .b(B), .out(subtractor_1_out), .bout(subtractor_1_bout));  // open: bin
  Multiplier #(.width(16)) multiplier_1 (.a(A), .b(B), .out(multiplier_1_out));  // open: cin, cout
  Divider #(.width(16)) divider_1 (.a(A), .b(B), .out(divider_1_out));  // open: upper, rem
  MUL_OVERFLOW_CHECK mul_overflow_check_1 (
    .A(A), .B(B), .Y(multiplier_1_out), .OVERFLOW(mul_overflow_check_1_overflow));
  Multiplexer #(.width(16), .disabled(0), .enable("false")) multiplexer_1 (
    .in0({16{1'b0}}), .in1(adder_1_out), .out(multiplexer_1_out), .sel(ADD));
  Multiplexer #(.width(16), .disabled(0), .enable("false")) multiplexer_2 (
    .in0({16{1'b0}}), .in1(subtractor_1_out), .out(multiplexer_2_out), .sel(SUB));
  Multiplexer #(.width(16), .disabled(0), .enable("false")) multiplexer_3 (
    .in0({16{1'b0}}), .in1(multiplier_1_out), .out(multiplexer_3_out), .sel(MUL));
  Multiplexer #(.width(16), .disabled(0), .enable("false")) multiplexer_4 (
    .in0({16{1'b0}}), .in1(divider_1_out), .out(multiplexer_4_out), .sel(DIV));
  assign Overflow = ADD ? adder_1_cout : 1'bz;  // Controlled_Buffer controlled_buffer_1
  Pull_Resistor pull_resistor_1 (.node(Overflow));
  assign Overflow = SUB ? subtractor_1_bout : 1'bz;  // Controlled_Buffer controlled_buffer_2
  assign Overflow = MUL ? mul_overflow_check_1_overflow : 1'bz;  // Controlled_Buffer controlled_buffer_3
  assign Y = multiplexer_1_out | multiplexer_2_out | multiplexer_3_out | multiplexer_4_out;  // OR_Gate or_1, 16 bits wide
endmodule

module ALU (
  input  PAS_A,
  input  PAS_B,
  input  NEG_A,
  input  NEG_B,
  input  NOT_A,
  input  NOT_B,
  input  AND,
  input  OR,
  input  XOR,
  input  ADD,
  input  SUB,
  input  MUL,
  input  DIV,
  input  [15:0] A,
  input  [15:0] B,
  output [15:0] Y,
  output OVERFLOW,
  output ZERO
);

  wire or_1_out, or_2_out;
  wire [15:0] arithmetic_1_y, logic_1_y, multiplexer_1_out, multiplexer_2_out, negator_1_y, negator_2_y;

  NEGATOR negator_1 (.A(A), .in_2(NEG_A), .Y(negator_1_y));
  NEGATOR negator_2 (.A(B), .in_2(NEG_B), .Y(negator_2_y));
  Multiplexer #(.width(16), .enable("false")) multiplexer_1 (.in0(A), .in1(B), .out(multiplexer_1_out), .sel(PAS_B));
  or or_1 (or_1_out, PAS_A, PAS_B);
  LOGIC logic_1 (
    .A(negator_1_y), .B(negator_2_y), .Y(logic_1_y), .NOT_B(NOT_B), .NOT(NOT_A), .AND(AND), .OR(OR), .XOR(XOR));
  ARITHMETIC arithmetic_1 (
    .A(negator_1_y), .B(negator_2_y), .Y(arithmetic_1_y), .Overflow(OVERFLOW), .ADD(ADD), .SUB(SUB),
    .MUL(MUL), .DIV(DIV));
  or or_2 (or_2_out, ADD, SUB, MUL, DIV);
  Multiplexer #(.width(16), .enable("false")) multiplexer_2 (
    .in0(logic_1_y), .in1(arithmetic_1_y), .out(multiplexer_2_out), .sel(or_2_out));
  Multiplexer #(.width(16), .enable("false")) multiplexer_3 (
    .in0(multiplexer_2_out), .in1(multiplexer_1_out), .out(Y), .sel(or_1_out));
  nor nor_1 (ZERO, Y[0], Y[1], Y[2], Y[3], Y[4], Y[5], Y[6], Y[7], Y[8], Y[9], Y[10], Y[11], Y[12], Y[13], Y[14], Y[15]);
endmodule

module FLAG_REG_FILE (
  input  OVERFLOW,
  input  ZERO,
  input  CLK,
  input  CLR,
  input  EN,
  output V,
  output Z
);

  D_Flip_Flop d_ff_1 (.clk(CLK), .D(OVERFLOW), .Q(V), .en(EN), .reset(CLR));  // open: Qn, preset
  D_Flip_Flop d_ff_2 (.clk(CLK), .D(ZERO), .Q(Z), .en(EN), .reset(CLR));  // open: Qn, preset
endmodule

module READ_CONTROL (
  input  [15:0] in_1,
  input  [15:0] in_2,
  input  [15:0] in_3,
  input  [15:0] in_4,
  input  [15:0] in_5,
  input  [15:0] in_6,
  input  [15:0] in_7,
  input  [15:0] in_8,
  input  [15:0] in_9,
  input  [15:0] in_10,
  input  [15:0] in_11,
  input  [15:0] in_12,
  input  [15:0] in_13,
  input  [15:0] in_14,
  input  [15:0] in_15,
  input  [15:0] in_16,
  input  [15:0] R1,
  input  [15:0] R0,
  output [15:0] Y0,
  output [15:0] Y1
);

  assign Y0 = R0[0] ? in_1 : 16'bz;  // Controlled_Buffer controlled_buffer_1
  assign Y0 = R0[1] ? in_2 : 16'bz;  // Controlled_Buffer controlled_buffer_2
  assign Y0 = R0[2] ? in_3 : 16'bz;  // Controlled_Buffer controlled_buffer_3
  assign Y0 = R0[3] ? in_4 : 16'bz;  // Controlled_Buffer controlled_buffer_4
  assign Y0 = R0[4] ? in_5 : 16'bz;  // Controlled_Buffer controlled_buffer_5
  assign Y0 = R0[5] ? in_6 : 16'bz;  // Controlled_Buffer controlled_buffer_6
  assign Y0 = R0[6] ? in_7 : 16'bz;  // Controlled_Buffer controlled_buffer_7
  assign Y0 = R0[7] ? in_8 : 16'bz;  // Controlled_Buffer controlled_buffer_8
  assign Y0 = R0[8] ? in_9 : 16'bz;  // Controlled_Buffer controlled_buffer_9
  assign Y0 = R0[9] ? in_10 : 16'bz;  // Controlled_Buffer controlled_buffer_10
  assign Y0 = R0[10] ? in_11 : 16'bz;  // Controlled_Buffer controlled_buffer_11
  assign Y0 = R0[11] ? in_12 : 16'bz;  // Controlled_Buffer controlled_buffer_12
  assign Y0 = R0[12] ? in_13 : 16'bz;  // Controlled_Buffer controlled_buffer_13
  assign Y0 = R0[13] ? in_14 : 16'bz;  // Controlled_Buffer controlled_buffer_14
  assign Y0 = R0[14] ? in_15 : 16'bz;  // Controlled_Buffer controlled_buffer_15
  assign Y0 = R0[15] ? in_16 : 16'bz;  // Controlled_Buffer controlled_buffer_16
  assign Y1 = R1[0] ? in_1 : 16'bz;  // Controlled_Buffer controlled_buffer_17
  assign Y1 = R1[1] ? in_2 : 16'bz;  // Controlled_Buffer controlled_buffer_18
  assign Y1 = R1[2] ? in_3 : 16'bz;  // Controlled_Buffer controlled_buffer_19
  assign Y1 = R1[3] ? in_4 : 16'bz;  // Controlled_Buffer controlled_buffer_20
  assign Y1 = R1[4] ? in_5 : 16'bz;  // Controlled_Buffer controlled_buffer_21
  assign Y1 = R1[5] ? in_6 : 16'bz;  // Controlled_Buffer controlled_buffer_22
  assign Y1 = R1[6] ? in_7 : 16'bz;  // Controlled_Buffer controlled_buffer_23
  assign Y1 = R1[7] ? in_8 : 16'bz;  // Controlled_Buffer controlled_buffer_24
  assign Y1 = R1[8] ? in_9 : 16'bz;  // Controlled_Buffer controlled_buffer_25
  assign Y1 = R1[9] ? in_10 : 16'bz;  // Controlled_Buffer controlled_buffer_26
  assign Y1 = R1[10] ? in_11 : 16'bz;  // Controlled_Buffer controlled_buffer_27
  assign Y1 = R1[11] ? in_12 : 16'bz;  // Controlled_Buffer controlled_buffer_28
  assign Y1 = R1[12] ? in_13 : 16'bz;  // Controlled_Buffer controlled_buffer_29
  assign Y1 = R1[13] ? in_14 : 16'bz;  // Controlled_Buffer controlled_buffer_30
  assign Y1 = R1[14] ? in_15 : 16'bz;  // Controlled_Buffer controlled_buffer_31
  assign Y1 = R1[15] ? in_16 : 16'bz;  // Controlled_Buffer controlled_buffer_32
  Pull_Resistor pull_resistor_1 (.node(Y0));
  Pull_Resistor pull_resistor_2 (.node(Y1));
endmodule

module REGISTER_FILE (
  input  [15:0] A,
  input  CLK,
  input  CLR,
  input  W_EN,
  input  R1_EN,
  input  R0_EN,
  input  [3:0] R0,
  input  [3:0] R1,
  output [15:0] Y0,
  output [15:0] Y1
);

  wire decoder_1_out0, decoder_1_out1, decoder_1_out2, decoder_1_out3, decoder_1_out4, decoder_1_out5,
       decoder_1_out6, decoder_1_out7, decoder_1_out8, decoder_1_out9, decoder_1_out10, decoder_1_out11,
       decoder_1_out12, decoder_1_out13, decoder_1_out14, decoder_1_out15;
  wire [15:0] decoder_2_out0, decoder_3_out0, register_1_q, register_2_q, register_3_q, register_4_q,
       register_5_q, register_6_q, register_7_q, register_8_q, register_9_q, register_10_q, register_11_q,
       register_12_q, register_13_q, register_14_q, register_15_q, register_16_q;

  Decoder #(.select(4), .disabled(0)) decoder_1 (
    .out0(decoder_1_out0), .out1(decoder_1_out1), .out2(decoder_1_out2), .out3(decoder_1_out3),
    .out4(decoder_1_out4), .out5(decoder_1_out5), .out6(decoder_1_out6), .out7(decoder_1_out7),
    .out8(decoder_1_out8), .out9(decoder_1_out9), .out10(decoder_1_out10), .out11(decoder_1_out11),
    .out12(decoder_1_out12), .out13(decoder_1_out13), .out14(decoder_1_out14), .out15(decoder_1_out15),
    .sel(R1), .en(W_EN));
  Register #(.width(16)) register_1 (.D(A), .en(decoder_1_out0), .Q(register_1_q), .clk(CLK), .clr(CLR));
  Register #(.width(16)) register_2 (.D(A), .en(decoder_1_out1), .Q(register_2_q), .clk(CLK), .clr(CLR));
  Register #(.width(16)) register_3 (.D(A), .en(decoder_1_out2), .Q(register_3_q), .clk(CLK), .clr(CLR));
  Register #(.width(16)) register_4 (.D(A), .en(decoder_1_out3), .Q(register_4_q), .clk(CLK), .clr(CLR));
  Register #(.width(16)) register_5 (.D(A), .en(decoder_1_out4), .Q(register_5_q), .clk(CLK), .clr(CLR));
  Register #(.width(16)) register_6 (.D(A), .en(decoder_1_out5), .Q(register_6_q), .clk(CLK), .clr(CLR));
  Register #(.width(16)) register_7 (.D(A), .en(decoder_1_out6), .Q(register_7_q), .clk(CLK), .clr(CLR));
  Register #(.width(16)) register_8 (.D(A), .en(decoder_1_out7), .Q(register_8_q), .clk(CLK), .clr(CLR));
  Register #(.width(16)) register_9 (.D(A), .en(decoder_1_out8), .Q(register_9_q), .clk(CLK), .clr(CLR));
  Register #(.width(16)) register_10 (.D(A), .en(decoder_1_out9), .Q(register_10_q), .clk(CLK), .clr(CLR));
  Register #(.width(16)) register_11 (.D(A), .en(decoder_1_out10), .Q(register_11_q), .clk(CLK), .clr(CLR));
  Register #(.width(16)) register_12 (.D(A), .en(decoder_1_out11), .Q(register_12_q), .clk(CLK), .clr(CLR));
  Register #(.width(16)) register_13 (.D(A), .en(decoder_1_out12), .Q(register_13_q), .clk(CLK), .clr(CLR));
  Register #(.width(16)) register_14 (.D(A), .en(decoder_1_out13), .Q(register_14_q), .clk(CLK), .clr(CLR));
  Register #(.width(16)) register_15 (.D(A), .en(decoder_1_out14), .Q(register_15_q), .clk(CLK), .clr(CLR));
  Register #(.width(16)) register_16 (.D(A), .en(decoder_1_out15), .Q(register_16_q), .clk(CLK), .clr(CLR));
  Decoder #(.select(4), .disabled(0)) decoder_2 (
    .out0(decoder_2_out0[0]), .out1(decoder_2_out0[1]), .out2(decoder_2_out0[2]), .out3(decoder_2_out0[3]),
    .out4(decoder_2_out0[4]), .out5(decoder_2_out0[5]), .out6(decoder_2_out0[6]), .out7(decoder_2_out0[7]),
    .out8(decoder_2_out0[8]), .out9(decoder_2_out0[9]), .out10(decoder_2_out0[10]),
    .out11(decoder_2_out0[11]), .out12(decoder_2_out0[12]), .out13(decoder_2_out0[13]),
    .out14(decoder_2_out0[14]), .out15(decoder_2_out0[15]), .sel(R0), .en(R0_EN));
  Decoder #(.select(4), .disabled(0)) decoder_3 (
    .out0(decoder_3_out0[0]), .out1(decoder_3_out0[1]), .out2(decoder_3_out0[2]), .out3(decoder_3_out0[3]),
    .out4(decoder_3_out0[4]), .out5(decoder_3_out0[5]), .out6(decoder_3_out0[6]), .out7(decoder_3_out0[7]),
    .out8(decoder_3_out0[8]), .out9(decoder_3_out0[9]), .out10(decoder_3_out0[10]),
    .out11(decoder_3_out0[11]), .out12(decoder_3_out0[12]), .out13(decoder_3_out0[13]),
    .out14(decoder_3_out0[14]), .out15(decoder_3_out0[15]), .sel(R1), .en(R1_EN));
  READ_CONTROL read_control_1 (
    .in_1(register_1_q), .in_2(register_2_q), .in_3(register_3_q), .in_4(register_4_q), .in_5(register_5_q),
    .in_6(register_6_q), .in_7(register_7_q), .in_8(register_8_q), .in_9(register_9_q),
    .in_10(register_10_q), .in_11(register_11_q), .in_12(register_12_q), .in_13(register_13_q),
    .in_14(register_14_q), .in_15(register_15_q), .in_16(register_16_q), .Y0(Y0), .Y1(Y1),
    .R1(decoder_3_out0), .R0(decoder_2_out0));
endmodule

module CONTROL (
  input  EXECUTE,
  input  CLK,
  input  CLR,
  input  [29:0] WORD,
  input  [15:0] ADDR_INPUT,
  input  [15:0] R0_INPUT,
  input  [15:0] R1_INPUT,
  input  [1:0] FLAGS,
  output [12:0] ALUOP,
  output ALU_CHECK,
  output [15:0] PCROM,
  output LD_REG,
  output R0_EN,
  output LD_ADDR,
  output [3:0] R0,
  output LD_OUTPUT,
  output [3:0] R1,
  output [15:0] OPERAND
);

  wire and_1_out, comparator_1_eq, comparator_1_gt, comparator_1_lt, decoder_1_out14, decoder_1_out15,
       decoder_1_out16, decoder_1_out17, decoder_1_out18, decoder_1_out19, decoder_1_out31, not_1_out,
       not_2_out, pull_resistor_1_node;
  wire [15:0] multiplexer_1_out;

  Comparator #(.width(16)) comparator_1 (
    .a(multiplexer_1_out), .b(R1_INPUT), .gt(comparator_1_gt), .eq(comparator_1_eq), .lt(comparator_1_lt));
  Pull_Resistor pull_resistor_1 (.node(pull_resistor_1_node));
  assign pull_resistor_1_node = decoder_1_out14 ? 1'b1 : 1'bz;  // Controlled_Buffer controlled_buffer_1
  assign pull_resistor_1_node = decoder_1_out15 ? comparator_1_eq : 1'bz;  // Controlled_Buffer controlled_buffer_2
  assign pull_resistor_1_node = decoder_1_out16 ? comparator_1_gt : 1'bz;  // Controlled_Buffer controlled_buffer_3
  assign pull_resistor_1_node = decoder_1_out17 ? comparator_1_lt : 1'bz;  // Controlled_Buffer controlled_buffer_4
  assign pull_resistor_1_node = decoder_1_out18 ? FLAGS[0] : 1'bz;  // Controlled_Buffer controlled_buffer_5
  assign pull_resistor_1_node = decoder_1_out19 ? FLAGS[1] : 1'bz;  // Controlled_Buffer controlled_buffer_6
  not not_1 (not_1_out, pull_resistor_1_node);
  Counter #(.width(16), .max('hffff)) counter_1 (
    .load(pull_resistor_1_node), .D(ADDR_INPUT), .count(not_1_out), .Q(PCROM), .clk(and_1_out), .clr(CLR));  // open: carry
  and and_1 (and_1_out, EXECUTE, not_2_out, CLK);
  Multiplexer #(.width(16), .disabled(0), .enable("false")) multiplexer_1 (
    .in0(WORD[29:14]), .in1(R0_INPUT), .out(multiplexer_1_out), .sel(WORD[5]));
  not not_2 (not_2_out, decoder_1_out31);
  Decoder #(.select(5), .disabled(0), .enable("false")) decoder_1 (
    .out1(ALUOP[0]), .out2(ALUOP[1]), .out3(ALUOP[2]), .out4(ALUOP[3]), .out5(ALUOP[4]), .out6(ALUOP[5]),
    .out7(ALUOP[6]), .out8(ALUOP[7]), .out9(ALUOP[8]), .out10(ALUOP[9]), .out11(ALUOP[10]),
    .out12(ALUOP[11]), .out13(ALUOP[12]), .out14(decoder_1_out14), .out15(decoder_1_out15),
    .out16(decoder_1_out16), .out17(decoder_1_out17), .out18(decoder_1_out18), .out19(decoder_1_out19),
    .out20(LD_REG), .out21(LD_ADDR), .out22(LD_OUTPUT), .out31(decoder_1_out31), .sel(WORD[4:0]));  // open: out0, out23, out24, out25, out26, out27, out28, out29, out30
  or or_1 (ALU_CHECK, ALUOP[0], ALUOP[1], ALUOP[2], ALUOP[3], ALUOP[4], ALUOP[5], ALUOP[6], ALUOP[7], ALUOP[8], ALUOP[9], ALUOP[10], ALUOP[11], ALUOP[12]);

  assign OPERAND = WORD[29:14];
  assign R0 = WORD[9:6];
  assign R0_EN = WORD[5];
  assign R1 = WORD[13:10];
endmodule

module BOB (
  input  EXECUTE,
  input  CLK,
  input  CLR,
  input  [29:0] WORD,
  output [15:0] out_5,
  output [15:0] PCROM
);

  wire alu_1_overflow, alu_1_zero, control_1_alu_check, control_1_ld_addr, control_1_ld_output,
       control_1_ld_reg, control_1_r0_en, controlled_buffer_1_out, or_1_out;
  wire [1:0] flag_reg_file_1_v;
  wire [3:0] control_1_r0, control_1_r1;
  wire [12:0] control_1_aluop;
  wire [15:0] alu_1_y, control_1_operand, multiplexer_1_out, multiplexer_2_out, register_1_q,
       register_file_1_y0, register_file_1_y1;

  assign controlled_buffer_1_out = EXECUTE ? CLK : 1'bz;  // Controlled_Buffer controlled_buffer_1
  Pull_Resistor pull_resistor_1 (.node(controlled_buffer_1_out));
  CONTROL control_1 (
    .EXECUTE(EXECUTE), .CLK(controlled_buffer_1_out), .CLR(CLR), .WORD(WORD), .ALUOP(control_1_aluop),
    .ALU_CHECK(control_1_alu_check), .PCROM(PCROM), .R0_EN(control_1_r0_en), .R0(control_1_r0),
    .R1(control_1_r1), .OPERAND(control_1_operand), .ADDR_INPUT(register_1_q), .R0_INPUT(register_file_1_y0),
    .FLAGS(flag_reg_file_1_v), .R1_INPUT(register_file_1_y1), .LD_ADDR(control_1_ld_addr),
    .LD_REG(control_1_ld_reg), .LD_OUTPUT(control_1_ld_output));
  Register #(.width(16)) register_1 (
    .D(multiplexer_2_out), .en(control_1_ld_addr), .Q(register_1_q), .clk(controlled_buffer_1_out), .clr(CLR));
  Multiplexer #(.width(16), .disabled(0), .enable("false")) multiplexer_1 (
    .in0(multiplexer_2_out), .in1(alu_1_y), .out(multiplexer_1_out), .sel(control_1_alu_check));
  Multiplexer #(.width(16), .disabled(0), .enable("false")) multiplexer_2 (
    .in0(control_1_operand), .in1(register_file_1_y0), .out(multiplexer_2_out), .sel(control_1_r0_en));
  REGISTER_FILE register_file_1 (
    .A(multiplexer_1_out), .CLK(controlled_buffer_1_out), .CLR(CLR), .Y0(register_file_1_y0),
    .W_EN(or_1_out), .R0(control_1_r0), .R1(control_1_r1), .R0_EN(control_1_r0_en), .Y1(register_file_1_y1),
    .R1_EN(1'b1));
  or or_1 (or_1_out, control_1_ld_reg, control_1_alu_check);
  ALU alu_1 (
    .A(multiplexer_2_out), .B(register_file_1_y1), .Y(alu_1_y), .OVERFLOW(alu_1_overflow),
    .PAS_A(control_1_aluop[0]), .PAS_B(control_1_aluop[1]), .NEG_A(control_1_aluop[2]),
    .NEG_B(control_1_aluop[3]), .NOT_A(control_1_aluop[4]), .NOT_B(control_1_aluop[5]),
    .AND(control_1_aluop[6]), .OR(control_1_aluop[7]), .XOR(control_1_aluop[8]), .ADD(control_1_aluop[9]),
    .SUB(control_1_aluop[10]), .MUL(control_1_aluop[11]), .DIV(control_1_aluop[12]), .ZERO(alu_1_zero));
  FLAG_REG_FILE flag_reg_file_1 (
    .OVERFLOW(alu_1_overflow), .ZERO(alu_1_zero), .CLK(controlled_buffer_1_out), .CLR(CLR),
    .EN(control_1_alu_check), .V(flag_reg_file_1_v[0]), .Z(flag_reg_file_1_v[1]));
  Register #(.width(16)) register_2 (
    .D(multiplexer_2_out), .en(control_1_ld_output), .Q(out_5), .clk(controlled_buffer_1_out), .clr(CLR));
endmodule
