// Logisim project Lock.circ as structural Verilog: 1 circuit, main circuit main
module main (
  input  [7:0] in_1,
  input  [1:0] in_2
);

  wire button_1_out, comparator_1_eq, d_ff_1_q, not_1_out;
  wire [7:0] rom_1_data;

  ROM #(.addrWidth(2)) rom_1 (.addr(in_2), .data(rom_1_data));  // open: sel
  Hex_Digit_Display hex_digit_display_1 (.value(in_1[3:0]));  // open: dp
  Hex_Digit_Display hex_digit_display_2 (.value(in_1[7:4]));  // open: dp
  Comparator comparator_1 (.a(in_1), .b(rom_1_data), .eq(comparator_1_eq));  // open: gt, lt
  Button button_1 (.out(button_1_out));
  LED led_1 (.in(d_ff_1_q));
  LED led_2 (.in(not_1_out));
  not not_1 (not_1_out, d_ff_1_q);
  D_Flip_Flop d_ff_1 (.clk(button_1_out), .D(comparator_1_eq), .Q(d_ff_1_q));  // open: Qn, preset, en, reset

  // Notes on the sheet:
  //   Input
  //   Key
  //   contents of rom_1 (hex, n*v repeats v):
  //   c4 42 ba be
  //   Submit
endmodule
