// Logisim project MIPS cpu fail.circ as structural Verilog: 3 circuits, main circuit main
module main (
  input  Reset
);

  wire clock_1_out, comparator_1_eq, not_1_out;
  wire [3:0] controlled_buffer_1_out, counter_1_q;
  wire [5:4] controlled_buffer_1_out_2;
  wire [7:0] alu_1_output, registers_1_a, registers_1_b;
  wire [31:0] rom_1_data;

  Clock clock_1 (.out(clock_1_out));
  not not_1 (not_1_out, comparator_1_eq);
  Counter #(.width(4), .max('hf)) counter_1 (
    .load(comparator_1_eq), .D(controlled_buffer_1_out), .count(not_1_out), .Q(counter_1_q), .clk(clock_1_out));  // open: carry, clr
  ROM #(.addrWidth(4), .dataWidth(32)) rom_1 (.addr(counter_1_q), .data(rom_1_data));  // open: sel
  Registers registers_1 (
    .Write_reg(rom_1_data[20:16]), .Clock(clock_1_out), .A_reg(rom_1_data[10:6]), .B_reg(rom_1_data[15:11]),
    .Data(alu_1_output), .A(registers_1_a), .B(registers_1_b), .Reset(Reset));
  Comparator #(.width(6)) comparator_1 (.a(rom_1_data[5:0]), .b(6'b001001), .eq(comparator_1_eq));  // open: gt, lt
  assign {controlled_buffer_1_out_2, controlled_buffer_1_out} = comparator_1_eq ? rom_1_data[31:26] : 6'bz;  // Controlled_Buffer controlled_buffer_1
  ALU alu_1 (
    .A(registers_1_a), .B(registers_1_b), .Opcode(rom_1_data[5:0]), .shift_amt(rom_1_data[25:21]),
    .Output(alu_1_output));  // open: Overflow
  Pull_Resistor pull_resistor_1 (.node(alu_1_output));
  Hex_Digit_Display hex_digit_display_1 (.value(alu_1_output[3:0]));  // open: dp
  Hex_Digit_Display hex_digit_display_2 (.value(alu_1_output[7:4]));  // open: dp

  // Notes on the sheet:
  //   Opcode(6) RegA(5) RegB(5) RegC(5) Shamt (5) Function(6)
  //   31 to 0
  //   contents of rom_1 (hex, n*v repeats v):
  //   1 10001 10011000 200000 400800 24000002
endmodule

module ALU (
  input  [7:0] A,
  input  [7:0] B,
  input  [5:0] Opcode,
  input  [4:0] shift_amt,
  output [7:0] Output,
  output Overflow
);

  wire adder_1_cout, or_2_out, subtractor_1_bout;
  wire [7:0] adder_1_out, and_1_out, divider_1_out, multiplexer_1_out, multiplier_1_cout, or_1_out,
       shifter_1_out, shifter_2_out, subtractor_1_out, xor_1_out;

  assign and_1_out = A & B;  // AND_Gate and_1, 8 bits wide
  assign or_1_out = A | B;  // OR_Gate or_1, 8 bits wide
  assign xor_1_out = A ^ B;  // XOR_Gate xor_1, 8 bits wide
  Adder adder_1 (.a(A), .b(B), .out(adder_1_out), .cout(adder_1_cout));  // open: cin
  Subtractor subtractor_1 (.a(A), .b(B), .out(subtractor_1_out), .bout(subtractor_1_bout));  // open: bin
  Multiplier multiplier_1 (.a(A), .b(B), .cout(multiplier_1_cout));  // open: out, cin
  Divider divider_1 (.a(A), .b(B), .out(divider_1_out));  // open: upper, rem
  Shifter shifter_1 (.in(A), .\dist (3'b001), .out(shifter_1_out));
  Shifter #(.shift("lr")) shifter_2 (.in(A), .\dist (3'b001), .out(shifter_2_out));
  or or_2 (or_2_out, multiplier_1_cout[0], multiplier_1_cout[1], multiplier_1_cout[2], multiplier_1_cout[3], multiplier_1_cout[4], multiplier_1_cout[5], multiplier_1_cout[6], multiplier_1_cout[7]);
  Multiplexer #(.select(4), .width(8), .enable("false")) multiplexer_1 (
    .in0(A), .in1(and_1_out), .in2(or_1_out), .in3(xor_1_out), .in4(adder_1_out), .in5(subtractor_1_out),
    .in6(divider_1_out), .in7(shifter_1_out), .in8(shifter_2_out), .out(multiplexer_1_out), .sel(Opcode[3:0]));  // open: in9, in10, in11, in12, in13, in14, in15
  or or_3 (Overflow, adder_1_cout, subtractor_1_bout, or_2_out);
  Pull_Resistor pull_resistor_1 (.node(Output));
  Shifter #(.shift("rl")) shifter_3 (.in(multiplexer_1_out), .\dist (shift_amt[2:0]), .out(Output));
endmodule

// Reg
module Registers (
  input  [7:0] Data,
  input  [4:0] Write_reg,
  input  Reset,
  input  Clock,
  input  [4:0] A_reg,
  input  [4:0] B_reg,
  output [7:0] A,
  output [7:0] B
);

  wire decoder_1_out0, decoder_1_out1, decoder_1_out2, decoder_1_out3, decoder_1_out4, decoder_1_out5,
       decoder_1_out6, decoder_1_out7;
  wire [7:0] demultiplexer_1_out0, demultiplexer_1_out1, demultiplexer_1_out2, demultiplexer_1_out3,
       demultiplexer_1_out4, demultiplexer_1_out5, demultiplexer_1_out6, demultiplexer_1_out7, register_1_q,
       register_2_q, register_3_q, register_4_q, register_5_q, register_6_q, register_7_q, register_8_q;

  Demultiplexer #(.select(3), .width(8)) demultiplexer_1 (
    .out0(demultiplexer_1_out0), .out1(demultiplexer_1_out1), .out2(demultiplexer_1_out2),
    .out3(demultiplexer_1_out3), .out4(demultiplexer_1_out4), .out5(demultiplexer_1_out5),
    .out6(demultiplexer_1_out6), .out7(demultiplexer_1_out7), .in(Data), .sel(Write_reg[2:0]));  // open: en
  Decoder #(.select(3)) decoder_1 (
    .out0(decoder_1_out0), .out1(decoder_1_out1), .out2(decoder_1_out2), .out3(decoder_1_out3),
    .out4(decoder_1_out4), .out5(decoder_1_out5), .out6(decoder_1_out6), .out7(decoder_1_out7),
    .sel(Write_reg[2:0]));  // open: en
  Register register_1 (.D(demultiplexer_1_out0), .Q(register_1_q), .clk(decoder_1_out0), .clr(Reset));  // open: en
  Register register_2 (.D(demultiplexer_1_out1), .Q(register_2_q), .clk(decoder_1_out1), .clr(Reset));  // open: en
  Register register_3 (.D(demultiplexer_1_out2), .Q(register_3_q), .clk(decoder_1_out2), .clr(Reset));  // open: en
  Register register_4 (.D(demultiplexer_1_out3), .Q(register_4_q), .clk(decoder_1_out3), .clr(Reset));  // open: en
  Multiplexer #(.select(3), .width(8)) multiplexer_1 (
    .in0(register_1_q), .in1(register_2_q), .in2(register_3_q), .in3(register_4_q), .in4(register_5_q),
    .in5(register_6_q), .in6(register_7_q), .in7(register_8_q), .out(A), .sel(A_reg[2:0]));  // open: en
  Register register_5 (.D(demultiplexer_1_out4), .Q(register_5_q), .clk(decoder_1_out4), .clr(Reset));  // open: en
  Register register_6 (.D(demultiplexer_1_out5), .Q(register_6_q), .clk(decoder_1_out5), .clr(Reset));  // open: en
  Register register_7 (.D(demultiplexer_1_out6), .Q(register_7_q), .clk(decoder_1_out6), .clr(Reset));  // open: en
  Register register_8 (.D(demultiplexer_1_out7), .Q(register_8_q), .clk(decoder_1_out7), .clr(Reset));  // open: en
  Multiplexer #(.select(3), .width(8)) multiplexer_2 (
    .in0(register_1_q), .in1(register_2_q), .in2(register_3_q), .in3(register_4_q), .in4(register_5_q),
    .in5(register_6_q), .in6(register_7_q), .in7(register_8_q), .out(B), .sel(B_reg[2:0]));  // open: en
endmodule
