// Logisim project MIPS pipeline.circ as structural Verilog: 11 circuits, main circuit main
module main (
);

  wire branch_1_equal, clear_out, clock_out, decode_1_operand_0_select, decode_1_operand_1_select;
  wire [1:0] decode_1_branch_select__00_next__10_equal__11_unequal, forward_1_operand_0_select_2,
       forward_1_operand_1_select_2, id_ex_1_operand_0_select_2, id_ex_1_operand_1_select_2;
  wire [3:0] decode_1_operator_select, id_ex_1_operator_select_2;
  wire [4:0] decode_1_destination_register, ex_wb_1_destination_register_2, forward_1_destination_register_2,
       id_ex_1_destination_register_2;
  wire [15:0] adder_1_out, adder_2_out, id_ex_1_immediate_2, if_id_1_pc_4_2, multiplexer_1_out, PC__2_q;
  wire [31:0] alu_1_result, bit_extender_1_out, bit_extender_2_out, ex_wb_1_result_2, id_ex_1_regs_rs_2,
       id_ex_1_regs_rt_2, if_id_1_instruction_2, multiplexer_2_out, multiplexer_3_out, registers_1_v0,
       registers_1_value_0, registers_1_value_1, rom_1_data;

  Clock clock (.out(clock_out));
  Button clear (.out(clear_out));
  Register #(.width(16), .trigger("falling")) PC__2 (
    .D(multiplexer_1_out), .Q(PC__2_q), .clk(clock_out), .clr(clear_out));  // open: en
  Adder #(.width(16)) adder_1 (.a(PC__2_q), .b(16'h1), .out(adder_1_out));  // open: cin, cout
  Multiplexer #(.width(16)) multiplexer_1 (
    .in0(adder_1_out), .in1(adder_2_out), .out(multiplexer_1_out), .sel(branch_1_equal));  // open: en
  ROM #(.addrWidth(16), .dataWidth(32)) rom_1 (.addr(PC__2_q), .data(rom_1_data));  // open: sel
  IF_ID if_id_1 (
    .instruction(rom_1_data), .PC_4(adder_1_out), .instruction_2(if_id_1_instruction_2),
    .PC_4_2(if_id_1_pc_4_2), .clock(clock_out), .clear(clear_out));  // open: enable
  // Probe on registers_1_v0
  decode decode_1 (
    .instruction(if_id_1_instruction_2), .operand_0_select(decode_1_operand_0_select),
    .operand_1_select(decode_1_operand_1_select), .destination_register(decode_1_destination_register),
    .operator_select(decode_1_operator_select),
    .branch_select__00_next__10_equal__11_unequal(decode_1_branch_select__00_next__10_equal__11_unequal));
  registers registers_1 (
    .Read_0(if_id_1_instruction_2[25:21]), .Read_1(if_id_1_instruction_2[20:16]), .v0(registers_1_v0),
    .clear(clear_out), .write_value(ex_wb_1_result_2), .write_addr(ex_wb_1_destination_register_2),
    .clock(clock_out), .Value_0(registers_1_value_0), .Value_1(registers_1_value_1));
  Adder #(.width(16)) adder_2 (
    .a(if_id_1_pc_4_2), .b(if_id_1_instruction_2[15:0]), .out(adder_2_out));  // open: cin, cout
  forward forward_1 (
    .source_register_0(if_id_1_instruction_2[25:21]), .source_register_1(if_id_1_instruction_2[20:16]),
    .operand_0_select(decode_1_operand_0_select), .operand_1_select(decode_1_operand_1_select),
    .destination_register(decode_1_destination_register), .clock(clock_out),
    .operand_0_select_2(forward_1_operand_0_select_2), .operand_1_select_2(forward_1_operand_1_select_2),
    .destination_register_2(forward_1_destination_register_2));
  branch branch_1 (
    .source_0(registers_1_value_0), .source_1(registers_1_value_1),
    .branch_type(decode_1_branch_select__00_next__10_equal__11_unequal), .equal(branch_1_equal));
  ID_EX id_ex_1 (
    .immediate(if_id_1_instruction_2[15:0]), .operand_0_select(forward_1_operand_0_select_2),
    .operand_1_select(forward_1_operand_1_select_2), .destination_register(forward_1_destination_register_2),
    .operator_select(decode_1_operator_select), .regs_rs(registers_1_value_0), .regs_rt(registers_1_value_1),
    .immediate_2(id_ex_1_immediate_2), .operand_0_select_2(id_ex_1_operand_0_select_2),
    .operand_1_select_2(id_ex_1_operand_1_select_2), .destination_register_2(id_ex_1_destination_register_2),
    .operator_select_2(id_ex_1_operator_select_2), .regs_rs_2(id_ex_1_regs_rs_2),
    .regs_rt_2(id_ex_1_regs_rt_2), .clock(clock_out), .clear(clear_out));
  assign bit_extender_1_out = {{27{1'b0}}, id_ex_1_immediate_2[10:6]};  // Bit_Extender bit_extender_1
  assign bit_extender_2_out = {{16{id_ex_1_immediate_2[15]}}, id_ex_1_immediate_2};  // Bit_Extender bit_extender_2
  Multiplexer #(.select(2), .width(32)) multiplexer_2 (
    .in0(id_ex_1_regs_rs_2), .in1(bit_extender_1_out), .out(multiplexer_2_out),
    .sel(id_ex_1_operand_0_select_2));  // open: in2, in3, en
  Multiplexer #(.select(2), .width(32)) multiplexer_3 (
    .in0(id_ex_1_regs_rt_2), .in1(bit_extender_2_out), .out(multiplexer_3_out),
    .sel(id_ex_1_operand_1_select_2));  // open: in2, in3, en
  ALU alu_1 (
    .operand_0(multiplexer_2_out), .operand_1(multiplexer_3_out), .result(alu_1_result),
    .operation(id_ex_1_operator_select_2));
  EX_WB ex_wb_1 (
    .result(alu_1_result), .destination_register(id_ex_1_destination_register_2),
    .result_2(ex_wb_1_result_2), .destination_register_2(ex_wb_1_destination_register_2), .clock(clock_out),
    .clear(clear_out));

  // Notes on the sheet:
  //   Place your name(s) here
endmodule

module IF_ID (
  input  [31:0] instruction,
  input  [15:0] PC_4,
  input  enable,
  input  clock,
  input  clear,
  output [31:0] instruction_2,
  output [15:0] PC_4_2
);


  assign instruction_2 = instruction;
  assign PC_4_2 = PC_4;
endmodule

// dcde
module decode (
  input  [31:0] instruction,
  output operand_0_select,
  output operand_1_select,
  output [4:0] destination_register,
  output [3:0] operator_select,
  output [1:0] branch_select__00_next__10_equal__11_unequal
);

  wire decode_i_type_1_valid, decode_r_type_1_opand, decode_r_type_1_valid;
  wire [1:0] decode_i_type_1_branch0;
  wire [3:0] decode_i_type_1_op0_2, decode_r_type_1_op0;
  wire [4:0] multiplexer_2_out;
  wire [4:4] multiplexer_3_out;

  decode_R_type decode_r_type_1 (
    .f5(instruction[5]), .f4(instruction[4]), .f3(instruction[3]), .f2(instruction[2]), .f1(instruction[1]),
    .f0(instruction[0]), .opand(decode_r_type_1_opand), .op3(decode_r_type_1_op0[3]),
    .op2(decode_r_type_1_op0[2]), .op1(decode_r_type_1_op0[1]), .op0(decode_r_type_1_op0[0]),
    .valid(decode_r_type_1_valid));
  decode_I_type decode_i_type_1 (
    .op5(instruction[31]), .op4(instruction[30]), .op3(instruction[29]), .op2(instruction[28]),
    .op1(instruction[27]), .op0(instruction[26]), .op3_2(decode_i_type_1_op0_2[3]),
    .op2_2(decode_i_type_1_op0_2[2]), .op1_2(decode_i_type_1_op0_2[1]), .op0_2(decode_i_type_1_op0_2[0]),
    .valid(decode_i_type_1_valid), .branch1(decode_i_type_1_branch0[1]), .branch0(decode_i_type_1_branch0[0]));
  or or_1 (operand_1_select, 1'b0, instruction[26], instruction[27], instruction[28], instruction[29], instruction[30], instruction[31]);
  Multiplexer multiplexer_1 (
    .in0(decode_r_type_1_opand), .in1(1'b0), .out(operand_0_select), .sel(operand_1_select));  // open: en
  Multiplexer #(.width(5)) multiplexer_2 (
    .in0(instruction[15:11]), .in1(instruction[20:16]), .out(multiplexer_2_out), .sel(operand_1_select));  // open: en
  Multiplexer multiplexer_3 (
    .in0(decode_r_type_1_valid), .in1(decode_i_type_1_valid), .out(multiplexer_3_out[4]),
    .sel(operand_1_select));  // open: en
  Multiplexer #(.width(4)) multiplexer_4 (
    .in0(decode_r_type_1_op0), .in1(decode_i_type_1_op0_2), .out(operator_select), .sel(operand_1_select));  // open: en
  Multiplexer #(.width(2)) multiplexer_5 (
    .in0(2'b00), .in1(decode_i_type_1_branch0), .out(branch_select__00_next__10_equal__11_unequal),
    .sel(operand_1_select));  // open: en
  assign destination_register = multiplexer_2_out & {5{multiplexer_3_out[4]}};  // AND_Gate and_1, 5 bits wide
endmodule

module decode_R_type (
  input  f5,
  input  f4,
  input  f3,
  input  f2,
  input  f1,
  input  f0,
  output opand,
  output op3,
  output op2,
  output op1,
  output op0,
  output valid
);

  wire and_2_out, and_3_out, and_4_out, and_5_out, and_6_out, and_7_out, and_8_out, and_9_out, and_10_out,
       and_11_out, and_12_out, not_1_out, not_2_out, not_3_out, not_4_out, not_5_out, not_6_out, not_7_out,
       not_8_out, not_9_out, not_10_out, not_11_out, not_12_out, not_13_out, not_14_out;

  not not_1 (not_1_out, f3);
  not not_2 (not_2_out, f1);
  not not_3 (not_3_out, f0);
  not not_4 (not_4_out, f5);
  not not_5 (not_5_out, f2);
  not not_6 (not_6_out, f4);
  not not_7 (not_7_out, f3);
  not not_8 (not_8_out, f0);
  not not_9 (not_9_out, f4);
  not not_10 (not_10_out, f3);
  not not_11 (not_11_out, f4);
  not not_12 (not_12_out, f3);
  not not_13 (not_13_out, f4);
  not not_14 (not_14_out, f2);
  nor nor_1 (opand, f5, f4, f3, f2);
  and and_1 (op3, f5, not_1_out);
  and and_2 (and_2_out, f2, not_2_out, f0);
  and and_3 (and_3_out, f5, f2, not_3_out);
  and and_4 (and_4_out, not_4_out, f1);
  and and_5 (and_5_out, f2, f1);
  and and_6 (and_6_out, f1, f0);
  and and_7 (and_7_out, f2, f0);
  and and_8 (and_8_out, f5, not_5_out, f1);
  and and_9 (and_9_out, not_6_out, not_7_out, not_8_out);
  and and_10 (and_10_out, not_9_out, not_10_out, f1);
  and and_11 (and_11_out, f5, not_11_out, not_12_out);
  and and_12 (and_12_out, f5, not_13_out, not_14_out, f1);
  or or_1 (op2, and_2_out, f3, and_3_out);
  or or_2 (op1, and_4_out, and_5_out, f3);
  or or_3 (op0, and_6_out, and_7_out, and_8_out);
  or or_4 (valid, and_9_out, and_10_out, and_11_out, and_12_out);
endmodule

module decode_I_type (
  input  op5,
  input  op4,
  input  op3,
  input  op2,
  input  op1,
  input  op0,
  output op3_2,
  output op2_2,
  output op1_2,
  output op0_2,
  output valid,
  output branch1,
  output branch0
);

  wire and_1_out, and_2_out, not_1_out, not_2_out, not_3_out, not_4_out, not_5_out, not_6_out, not_7_out,
       not_8_out, not_9_out, not_10_out, not_11_out, not_12_out;

  not not_1 (not_1_out, op1);
  or or_1 (op2_2, op1, op2);
  not not_2 (not_2_out, op2);
  not not_3 (not_3_out, op5);
  not not_4 (not_4_out, op4);
  not not_5 (not_5_out, op5);
  not not_6 (not_6_out, op4);
  not not_7 (not_7_out, op3);
  not not_8 (not_8_out, op1);
  not not_9 (not_9_out, op5);
  not not_10 (not_10_out, op4);
  not not_11 (not_11_out, op3);
  not not_12 (not_12_out, op1);
  or or_2 (op3_2, not_1_out, op2);
  and and_1 (and_1_out, not_2_out, op1);
  and and_2 (and_2_out, op2, op0);
  and and_3 (valid, not_3_out, not_4_out, op3);
  and and_4 (branch1, not_5_out, not_6_out, not_7_out, op2, not_8_out);
  and and_5 (branch0, not_9_out, not_10_out, not_11_out, op2, not_12_out, op0);
  or or_3 (op0_2, and_1_out, and_2_out);

  assign op1_2 = op1;
endmodule

// regs
module registers (
  input  [4:0] Read_0,
  input  [4:0] Read_1,
  input  clear,
  input  [31:0] write_value,
  input  [4:0] write_addr,
  input  clock,
  output [31:0] v0,
  output [31:0] Value_0,
  output [31:0] Value_1
);

  wire decoder_1_out1, decoder_1_out2, decoder_1_out3, decoder_1_out4, decoder_1_out5, decoder_1_out6,
       decoder_1_out7, decoder_1_out8, decoder_1_out9, decoder_1_out10, decoder_1_out11, decoder_1_out12,
       decoder_1_out13, decoder_1_out14, decoder_1_out15, decoder_1_out16, decoder_1_out17, decoder_1_out18,
       decoder_1_out19, decoder_1_out20, decoder_1_out21, decoder_1_out22, decoder_1_out23, decoder_1_out24,
       decoder_1_out25, decoder_1_out26, decoder_1_out27, decoder_1_out28, decoder_1_out29, decoder_1_out30,
       decoder_1_out31;
  wire [31:0] a0_q, a1_q, a2_q, a3_q, at_q, fp_q, gp_q, k0_q, k1_q, ra_q, s0_q, s1_q, s2_q, s3_q, s4_q, s5_q,
       s6_q, s7_q, sp_q, t0_q, t1_q, t2_q, t3_q, t4_q, t5_q, t6_q, t7_q, t8_q, t9_q, v1_q;

  Decoder #(.select(5), .enable("false")) decoder_1 (
    .out1(decoder_1_out1), .out2(decoder_1_out2), .out3(decoder_1_out3), .out4(decoder_1_out4),
    .out5(decoder_1_out5), .out6(decoder_1_out6), .out7(decoder_1_out7), .out8(decoder_1_out8),
    .out9(decoder_1_out9), .out10(decoder_1_out10), .out11(decoder_1_out11), .out12(decoder_1_out12),
    .out13(decoder_1_out13), .out14(decoder_1_out14), .out15(decoder_1_out15), .out16(decoder_1_out16),
    .out17(decoder_1_out17), .out18(decoder_1_out18), .out19(decoder_1_out19), .out20(decoder_1_out20),
    .out21(decoder_1_out21), .out22(decoder_1_out22), .out23(decoder_1_out23), .out24(decoder_1_out24),
    .out25(decoder_1_out25), .out26(decoder_1_out26), .out27(decoder_1_out27), .out28(decoder_1_out28),
    .out29(decoder_1_out29), .out30(decoder_1_out30), .out31(decoder_1_out31), .sel(write_addr));  // open: out0
  Register #(.width(32)) at (.D(write_value), .en(decoder_1_out1), .Q(at_q), .clk(clock), .clr(clear));
  Register #(.width(32)) u_v0 (.D(write_value), .en(decoder_1_out2), .Q(v0), .clk(clock), .clr(clear));
  Register #(.width(32)) v1 (.D(write_value), .en(decoder_1_out3), .Q(v1_q), .clk(clock), .clr(clear));
  Register #(.width(32)) a0 (.D(write_value), .en(decoder_1_out4), .Q(a0_q), .clk(clock), .clr(clear));
  Register #(.width(32)) a1 (.D(write_value), .en(decoder_1_out5), .Q(a1_q), .clk(clock), .clr(clear));
  Register #(.width(32)) a2 (.D(write_value), .en(decoder_1_out6), .Q(a2_q), .clk(clock), .clr(clear));
  Register #(.width(32)) a3 (.D(write_value), .en(decoder_1_out7), .Q(a3_q), .clk(clock), .clr(clear));
  Register #(.width(32)) t0 (.D(write_value), .en(decoder_1_out8), .Q(t0_q), .clk(clock), .clr(clear));
  Register #(.width(32)) t1 (.D(write_value), .en(decoder_1_out9), .Q(t1_q), .clk(clock), .clr(clear));
  Register #(.width(32)) t2 (.D(write_value), .en(decoder_1_out10), .Q(t2_q), .clk(clock), .clr(clear));
  Register #(.width(32)) t3 (.D(write_value), .en(decoder_1_out11), .Q(t3_q), .clk(clock), .clr(clear));
  Register #(.width(32)) t4 (.D(write_value), .en(decoder_1_out12), .Q(t4_q), .clk(clock), .clr(clear));
  Register #(.width(32)) t5 (.D(write_value), .en(decoder_1_out13), .Q(t5_q), .clk(clock), .clr(clear));
  Register #(.width(32)) t6 (.D(write_value), .en(decoder_1_out14), .Q(t6_q), .clk(clock), .clr(clear));
  Register #(.width(32)) t7 (.D(write_value), .en(decoder_1_out15), .Q(t7_q), .clk(clock), .clr(clear));
  Register #(.width(32)) s0 (.D(write_value), .en(decoder_1_out16), .Q(s0_q), .clk(clock), .clr(clear));
  Register #(.width(32)) s1 (.D(write_value), .en(decoder_1_out17), .Q(s1_q), .clk(clock), .clr(clear));
  Register #(.width(32)) s2 (.D(write_value), .en(decoder_1_out18), .Q(s2_q), .clk(clock), .clr(clear));
  Register #(.width(32)) s3 (.D(write_value), .en(decoder_1_out19), .Q(s3_q), .clk(clock), .clr(clear));
  Register #(.width(32)) s4 (.D(write_value), .en(decoder_1_out20), .Q(s4_q), .clk(clock), .clr(clear));
  Register #(.width(32)) s5 (.D(write_value), .en(decoder_1_out21), .Q(s5_q), .clk(clock), .clr(clear));
  Register #(.width(32)) s6 (.D(write_value), .en(decoder_1_out22), .Q(s6_q), .clk(clock), .clr(clear));
  Register #(.width(32)) s7 (.D(write_value), .en(decoder_1_out23), .Q(s7_q), .clk(clock), .clr(clear));
  Register #(.width(32)) t8 (.D(write_value), .en(decoder_1_out24), .Q(t8_q), .clk(clock), .clr(clear));
  Register #(.width(32)) t9 (.D(write_value), .en(decoder_1_out25), .Q(t9_q), .clk(clock), .clr(clear));
  Register #(.width(32)) k0 (.D(write_value), .en(decoder_1_out26), .Q(k0_q), .clk(clock), .clr(clear));
  Register #(.width(32)) k1 (.D(write_value), .en(decoder_1_out27), .Q(k1_q), .clk(clock), .clr(clear));
  Register #(.width(32)) gp (.D(write_value), .en(decoder_1_out28), .Q(gp_q), .clk(clock), .clr(clear));
  Register #(.width(32)) sp (.D(write_value), .en(decoder_1_out29), .Q(sp_q), .clk(clock), .clr(clear));
  Register #(.width(32)) fp (.D(write_value), .en(decoder_1_out30), .Q(fp_q), .clk(clock), .clr(clear));
  Register #(.width(32)) ra (.D(write_value), .en(decoder_1_out31), .Q(ra_q), .clk(clock), .clr(clear));
  Multiplexer #(.select(5), .width(32)) multiplexer_1 (
    .in0({32{1'b0}}), .in1(at_q), .in2(v0), .in3(v1_q), .in4(a0_q), .in5(a1_q), .in6(a2_q), .in7(a3_q),
    .in8(t0_q), .in9(t1_q), .in10(t2_q), .in11(t3_q), .in12(t4_q), .in13(t5_q), .in14(t6_q), .in15(t7_q),
    .in16(s0_q), .in17(s1_q), .in18(s2_q), .in19(s3_q), .in20(s4_q), .in21(s5_q), .in22(s6_q), .in23(s7_q),
    .in24(t8_q), .in25(t9_q), .in26(k0_q), .in27(k1_q), .in28(gp_q), .in29(sp_q), .in30(fp_q), .in31(ra_q),
    .out(Value_0), .sel(Read_0));  // open: en
  Multiplexer #(.select(5), .width(32)) multiplexer_2 (
    .in0({32{1'b0}}), .in1(at_q), .in2(v0), .in3(v1_q), .in4(a0_q), .in5(a1_q), .in6(a2_q), .in7(a3_q),
    .in8(t0_q), .in9(t1_q), .in10(t2_q), .in11(t3_q), .in12(t4_q), .in13(t5_q), .in14(t6_q), .in15(t7_q),
    .in16(s0_q), .in17(s1_q), .in18(s2_q), .in19(s3_q), .in20(s4_q), .in21(s5_q), .in22(s6_q), .in23(s7_q),
    .in24(t8_q), .in25(t9_q), .in26(k0_q), .in27(k1_q), .in28(gp_q), .in29(sp_q), .in30(fp_q), .in31(ra_q),
    .out(Value_1), .sel(Read_1));  // open: en
endmodule

// fwrd
module forward (
  input  [4:0] source_register_0,
  input  [4:0] source_register_1,
  input  operand_0_select,
  input  operand_1_select,
  input  [4:0] destination_register,
  input  clock,
  output [1:0] operand_0_select_2,
  output [1:0] operand_1_select_2,
  output [4:0] destination_register_2
);


  assign destination_register_2 = destination_register;
  assign operand_0_select_2 = {1'b0, operand_0_select};
  assign operand_1_select_2 = {1'b0, operand_1_select};
endmodule

// brch
module branch (
  input  [1:0] branch_type,
  input  [31:0] source_0,
  input  [31:0] source_1,
  output equal
);

  wire not_1_out, or_1_out, xor_2_out;
  wire [31:0] xor_1_out;

  assign xor_1_out = source_0 ^ source_1;  // XOR_Gate xor_1, 32 bits wide
  not not_1 (not_1_out, or_1_out);
  or or_1 (or_1_out, xor_1_out[0], xor_1_out[1], xor_1_out[2], xor_1_out[3], xor_1_out[4], xor_1_out[5], xor_1_out[6], xor_1_out[7], xor_1_out[8], xor_1_out[9], xor_1_out[10], xor_1_out[11], xor_1_out[12], xor_1_out[13], xor_1_out[14], xor_1_out[15], xor_1_out[17], xor_1_out[18], xor_1_out[19], xor_1_out[20], xor_1_out[21], xor_1_out[22], xor_1_out[23], xor_1_out[24], xor_1_out[25], xor_1_out[26], xor_1_out[27], xor_1_out[28], xor_1_out[29], xor_1_out[30], xor_1_out[31], xor_1_out[16]);
  xor xor_2 (xor_2_out, branch_type[0], not_1_out);
  and and_1 (equal, branch_type[1], xor_2_out);
endmodule

module ID_EX (
  input  [15:0] immediate,
  input  [1:0] operand_0_select,
  input  [1:0] operand_1_select,
  input  [4:0] destination_register,
  input  [3:0] operator_select,
  input  [31:0] regs_rs,
  input  [31:0] regs_rt,
  input  clock,
  input  clear,
  output [15:0] immediate_2,
  output [1:0] operand_0_select_2,
  output [1:0] operand_1_select_2,
  output [4:0] destination_register_2,
  output [3:0] operator_select_2,
  output [31:0] regs_rs_2,
  output [31:0] regs_rt_2
);


  assign destination_register_2 = destination_register;
  assign immediate_2 = immediate;
  assign operand_0_select_2 = operand_0_select;
  assign operand_1_select_2 = operand_1_select;
  assign operator_select_2 = operator_select;
  assign regs_rs_2 = regs_rs;
  assign regs_rt_2 = regs_rt;
endmodule

module ALU (
  input  [31:0] operand_0,
  input  [31:0] operand_1,
  input  [3:0] operation,
  output [31:0] result
);

  wire [31:0] adder_1_out, and_1_out, bit_extender_1_out, nor_1_out, or_1_out, shifter_1_out, shifter_2_out,
       shifter_3_out, xor_1_out, xor_2_out;

  assign bit_extender_1_out = {{31{operation[0]}}, operation[0]};  // Bit_Extender bit_extender_1
  Shifter #(.width(32)) shifter_1 (.in(operand_1), .\dist (operand_0[4:0]), .out(shifter_1_out));
  Shifter #(.width(32), .shift("lr")) shifter_2 (.in(operand_1), .\dist (operand_0[4:0]), .out(shifter_2_out));
  Shifter #(.width(32), .shift("ar")) shifter_3 (.in(operand_1), .\dist (operand_0[4:0]), .out(shifter_3_out));
  Adder #(.width(32)) adder_1 (.a(operand_0), .b(xor_1_out), .out(adder_1_out), .cin(operation[0]));  // open: cout
  assign xor_1_out = operand_1 ^ bit_extender_1_out;  // XOR_Gate xor_1, 32 bits wide
  assign nor_1_out = ~(operand_0 | operand_1);  // NOR_Gate nor_1, 32 bits wide
  assign and_1_out = operand_0 & operand_1;  // AND_Gate and_1, 32 bits wide
  assign or_1_out = operand_0 | operand_1;  // OR_Gate or_1, 32 bits wide
  assign xor_2_out = operand_0 ^ operand_1;  // XOR_Gate xor_2, 32 bits wide
  Multiplexer #(.select(4), .width(32)) multiplexer_1 (
    .in0(shifter_1_out), .in2(shifter_2_out), .in3(shifter_3_out), .in7(adder_1_out), .in8(adder_1_out),
    .in9(adder_1_out), .in11(nor_1_out), .in12(and_1_out), .in13(or_1_out), .in14(xor_2_out),
    .in15({operand_1[15:0], {16{1'b0}}}), .out(result), .sel(operation));  // open: in1, in4, in5, in6, in10, en
endmodule

module EX_WB (
  input  [31:0] result,
  input  [4:0] destination_register,
  input  clock,
  input  clear,
  output [31:0] result_2,
  output [4:0] destination_register_2
);


  assign destination_register_2 = destination_register;
  assign result_2 = result;
endmodule
