// Logisim project RAM.circ as structural Verilog: 1 circuit, main circuit main
module main (
  input  [7:0] in_1,
  input  Store,
  input  [7:0] in_3,
  output [7:0] out_4
);

  wire clock_1_out, not_1_out;

  assign out_4 = Store ? in_1 : 8'bz;  // Controlled_Buffer controlled_buffer_1
  Clock clock_1 (.out(clock_1_out));
  not not_1 (not_1_out, Store);
  RAM ram_1 (.addr(in_3), .data(out_4), .clk(clock_1_out), .ld(not_1_out));  // open: sel, clr

  // Notes on the sheet:
  //   Load
  //   Address
  //   Store/load
endmodule
