// Logisim project adder subtractor.circ as structural Verilog: 1 circuit, main circuit main
module main (
  input  [3:0] A,
  input  [3:0] B,
  input  Add_Subtract,
  output [3:0] out_4,
  output out_5
);

  wire adder_1_cout;
  wire [3:0] xor_1_out;

  assign xor_1_out = B ^ {4{Add_Subtract}};  // XOR_Gate xor_1, 4 bits wide
  Adder #(.width(4)) adder_1 (.a(A), .b(xor_1_out), .out(out_4), .cin(Add_Subtract), .cout(adder_1_cout));
  xor xor_2 (out_5, adder_1_cout, Add_Subtract);
endmodule
