// Logisim project babylonian squareroot.circ as structural Verilog: 1 circuit, main circuit main
module main (
  input  [15:0] Original_Number,
  input  in_2,
  output [15:0] out_3
);

  wire clock_1_out;
  wire [15:0] adder_1_out, divider_1_out, multiplexer_1_out, register_1_q, shifter_1_out;

  Shifter #(.width(16), .shift("lr")) shifter_1 (.in(Original_Number), .\dist (4'b0001), .out(shifter_1_out));
  Multiplexer #(.width(16), .disabled(0), .enable("false")) multiplexer_1 (
    .in0(shifter_1_out), .in1(out_3), .out(multiplexer_1_out), .sel(in_2));
  Clock clock_1 (.out(clock_1_out));
  Register #(.width(16)) register_1 (.D(multiplexer_1_out), .Q(register_1_q), .clk(clock_1_out));  // open: en, clr
  Divider #(.width(16)) divider_1 (.a(Original_Number), .b(register_1_q), .out(divider_1_out));  // open: upper, rem
  Adder #(.width(16)) adder_1 (.a(divider_1_out), .b(register_1_q), .out(adder_1_out));  // open: cin, cout
  Shifter #(.width(16), .shift("lr")) shifter_2 (.in(adder_1_out), .\dist (4'b0001), .out(out_3));
endmodule
