// Logisim project carry save adder regular design.circ as structural Verilog: 1 circuit, main circuit main
module main (
  input  [7:0] in_1,
  input  [7:0] in_2,
  input  [7:0] in_3,
  output [7:0] out_4,
  output [7:0] out_5
);

  Adder #(.width(1)) adder_1 (.a(in_2[7]), .b(in_1[7]), .out(out_4[0]), .cin(in_3[7]), .cout(out_5[0]));
  Adder #(.width(1)) adder_2 (.a(in_2[6]), .b(in_1[6]), .out(out_4[1]), .cin(in_3[6]), .cout(out_5[1]));
  Adder #(.width(1)) adder_3 (.a(in_2[5]), .b(in_1[5]), .out(out_4[2]), .cin(in_3[5]), .cout(out_5[2]));
  Adder #(.width(1)) adder_4 (.a(in_2[4]), .b(in_1[4]), .out(out_4[3]), .cin(in_3[4]), .cout(out_5[3]));
  Adder #(.width(1)) adder_5 (.a(in_2[2]), .b(in_1[2]), .out(out_4[5]), .cin(in_3[2]), .cout(out_5[5]));
  Adder #(.width(1)) adder_6 (.a(in_2[3]), .b(in_1[3]), .out(out_4[4]), .cin(in_3[3]), .cout(out_5[4]));
  Adder #(.width(1)) adder_7 (.a(in_2[1]), .b(in_1[1]), .out(out_4[6]), .cin(in_3[1]), .cout(out_5[6]));
  Adder #(.width(1)) adder_8 (.a(in_2[0]), .b(in_1[0]), .out(out_4[7]), .cin(in_3[0]), .cout(out_5[7]));
endmodule
