// Logisim project clock.circ as structural Verilog: 2 circuits, main circuit main
module main (
);

  wire button_1_out, button_2_out, button_3_out, clock_1_out, counter_1_carry, counter_2_carry,
       counter_3_carry, counter_4_carry, hour_1_out_2, or_1_out, or_2_out, or_3_out;
  wire [2:0] controlled_buffer_1_out;
  wire [3:0] counter_1_q, counter_2_q, counter_3_q, counter_4_q, hour_1_out_3, hour_1_out_4;

  LED led_1 (.in(hour_1_out_2));
  Hex_Digit_Display hex_digit_display_1 (.value(hour_1_out_3));  // open: dp
  hour hour_1 (.out_2(hour_1_out_2), .out_3(hour_1_out_3), .out_4(hour_1_out_4), .in_1(or_1_out));
  Button button_1 (.out(button_1_out));
  DotMatrix #(.matrixcols(1), .matrixrows(3)) dotmatrix_1 (.col0(3'b101));
  Hex_Digit_Display hex_digit_display_2 (.value(hour_1_out_4));  // open: dp
  Counter #(.width(4), .max('h5), .trigger("falling")) counter_1 (
    .Q(counter_1_q), .carry(counter_1_carry), .clk(counter_2_carry));  // open: load, D, count, clr
  or or_1 (or_1_out, counter_1_carry, button_1_out);
  Hex_Digit_Display hex_digit_display_3 (.value(counter_1_q));  // open: dp
  Hex_Digit_Display hex_digit_display_4 (.value(counter_2_q));  // open: dp
  Counter #(.width(4), .max('h9)) counter_2 (
    .Q(counter_2_q), .carry(counter_2_carry), .clk(or_2_out));  // open: load, D, count, clr
  or or_2 (or_2_out, counter_3_carry, button_2_out);
  Button button_2 (.out(button_2_out));
  DotMatrix #(.matrixcols(1), .matrixrows(3)) dotmatrix_2 (.col0(controlled_buffer_1_out));
  Hex_Digit_Display hex_digit_display_5 (.value(counter_3_q));  // open: dp
  Counter #(.width(4), .max('h5), .trigger("falling")) counter_3 (
    .Q(counter_3_q), .carry(counter_3_carry), .clk(counter_4_carry));  // open: load, D, count, clr
  Hex_Digit_Display hex_digit_display_6 (.value(counter_4_q));  // open: dp
  assign controlled_buffer_1_out = clock_1_out ? 3'b101 : 3'bz;  // Controlled_Buffer controlled_buffer_1
  Pull_Resistor pull_resistor_1 (.node(controlled_buffer_1_out));
  Counter #(.width(4), .max('h9)) counter_4 (
    .Q(counter_4_q), .carry(counter_4_carry), .clk(or_3_out));  // open: load, D, count, clr
  or or_3 (or_3_out, clock_1_out, button_3_out);
  Button button_3 (.out(button_3_out));
  Clock clock_1 (.out(clock_1_out));

  // Notes on the sheet:
  //   PM
  //   Clock, by Jason Xu
  //   trigger is falling edge
  //   2 tick frequency
endmodule

module hour (
  input  in_1,
  output out_2,
  output [3:0] out_3,
  output [3:0] out_4
);

  wire counter_1_carry;
  wire [3:0] counter_1_q;

  Counter #(.width(4), .max('hb), .trigger("falling")) counter_1 (
    .Q(counter_1_q), .carry(counter_1_carry), .clk(in_1));  // open: load, D, count, clr
  T_Flip_Flop #(.trigger("falling")) t_ff_1 (
    .clk(counter_1_carry), .T(1'b1), .Q(out_2));  // open: Qn, preset, reset, en
  ROM #(.addrWidth(4)) rom_1 (.addr(counter_1_q), .data({out_3, out_4}));  // open: sel

  // Notes on the sheet:
  //   ROM is numbers 12, 01-11
  //   contents of rom_1 (hex, n*v repeats v):
  //   12 1 2 3 4 5 6 7 8 9 10 11
endmodule
