// Logisim project decimal counter.circ as structural Verilog: 2 circuits, main circuit main
module main (
  output out_1
);

  wire button_1_out, clock_1_out, dec_counter_1_rollover, dec_counter_3_rollover;
  wire [3:0] dec_counter_1_out_3, dec_counter_2_out_3, dec_counter_3_out_3;

  Hex_Digit_Display hex_digit_display_1 (.value(dec_counter_1_out_3));  // open: dp
  Hex_Digit_Display hex_digit_display_2 (.value(dec_counter_2_out_3));  // open: dp
  Dec_counter dec_counter_1 (
    .count(dec_counter_3_rollover), .out_3(dec_counter_1_out_3), .clear(button_1_out),
    .rollover(dec_counter_1_rollover));
  Dec_counter dec_counter_2 (
    .count(dec_counter_1_rollover), .out_3(dec_counter_2_out_3), .clear(button_1_out), .rollover(out_1));
  Hex_Digit_Display hex_digit_display_3 (.value(dec_counter_3_out_3));  // open: dp
  Dec_counter dec_counter_3 (
    .count(clock_1_out), .out_3(dec_counter_3_out_3), .clear(button_1_out), .rollover(dec_counter_3_rollover));
  Clock clock_1 (.out(clock_1_out));
  Button button_1 (.out(button_1_out));
endmodule

module Dec_counter (
  input  count,
  input  clear,
  output [3:0] out_3,
  output rollover
);

  wire counter_1_carry;

  Counter #(.width(4), .max('h9)) counter_1 (
    .Q(out_3), .carry(counter_1_carry), .clk(count), .clr(clear));  // open: load, D, count
  D_Flip_Flop d_ff_1 (.clk(count), .D(counter_1_carry), .Q(rollover));  // open: Qn, preset, en, reset
endmodule
