// Logisim project encrypt.circ as structural Verilog: 2 circuits, main circuit main
module main (
  input  [6:0] Key,
  input  [6:0] Key_2
);

  wire button_1_out, button_2_out, button_3_out, clock_1_out, clock_2_out, clock_3_out;
  wire [6:0] keyboard_1_data, xor_1_out, xor_2_out;

  Keyboard #(.buflen(8)) keyboard_1 (.clk(clock_1_out), .clr(button_1_out), .data(keyboard_1_data));  // open: re, avail
  Clock clock_1 (.out(clock_1_out));
  Button button_1 (.out(button_1_out));
  Clock clock_2 (.out(clock_2_out));
  assign xor_1_out = keyboard_1_data ^ Key;  // XOR_Gate xor_1, 7 bits wide
  TTY #(.rows(2), .cols(16)) tty_1 (.data(xor_1_out), .clk(clock_2_out), .clr(button_2_out));  // open: we
  Button button_2 (.out(button_2_out));
  assign xor_2_out = xor_1_out ^ Key_2;  // XOR_Gate xor_2, 7 bits wide
  TTY #(.rows(2), .cols(16)) tty_2 (.data(xor_2_out), .clk(clock_3_out), .clr(button_3_out));  // open: we
  Button button_3 (.out(button_3_out));
  Clock clock_3 (.out(clock_3_out));

  // Notes on the sheet:
  //   Sender
  //   Public (guy with no key)
  //   Reciever
endmodule

module XOR (
  input  [15:0] in_1,
  input  [7:0] in_2,
  output [15:0] out_3
);

  assign out_3[7:0] = in_1[7:0] ^ in_2;  // XOR_Gate xor_1, 8 bits wide
  assign out_3[15:8] = in_1[15:8] ^ in_2;  // XOR_Gate xor_2, 8 bits wide
endmodule
