// Logisim project fibonacci.circ as structural Verilog: 1 circuit, main circuit main
module main (
  output out_1
);

  wire adder_1_cout, button_1_out, clock_1_out;
  wire [7:0] adder_1_out, n_1_q, n_2_q;

  Clock clock_1 (.out(clock_1_out));
  Button button_1 (.out(button_1_out));
  Register n_1 (.D(adder_1_out), .Q(n_1_q), .clk(clock_1_out), .clr(button_1_out));  // open: en
  Register n_2 (.D(n_1_q), .Q(n_2_q), .clk(clock_1_out), .clr(button_1_out));  // open: en
  Adder adder_1 (.a(n_2_q), .b(n_1_q), .out(adder_1_out), .cout(adder_1_cout));  // open: cin
  Hex_Digit_Display hex_digit_display_1 (.value(adder_1_out[7:4]));  // open: dp
  Hex_Digit_Display hex_digit_display_2 (.value(adder_1_out[3:0]));  // open: dp
  S_R_Flip_Flop s_r_ff_1 (
    .S(adder_1_cout), .clk(clock_1_out), .R(button_1_out), .Q(out_1));  // open: Qn, preset, reset, en
endmodule
