// Logisim project keyboard.circ as structural Verilog: 1 circuit, main circuit main
module main (
  input  Enable
);

  wire button_1_out, clock_1_out, keyboard_1_avail, not_1_out;
  wire [6:0] keyboard_1_data;

  Keyboard keyboard_1 (
    .clk(clock_1_out), .clr(not_1_out), .avail(keyboard_1_avail), .data(keyboard_1_data));  // open: re
  Clock clock_1 (.out(clock_1_out));
  not not_1 (not_1_out, Enable);
  TTY tty_1 (.data(keyboard_1_data), .clk(clock_1_out), .we(Enable), .clr(button_1_out));
  Button button_1 (.out(button_1_out));
  LED led_1 (.in(keyboard_1_avail));

  // Notes on the sheet:
  //   Clear
  //   still entering
endmodule
