// Logisim project kogge stone.circ as structural Verilog: 3 circuits, main circuit main
module main (
  input  A3,
  input  B3,
  input  A2,
  input  B2,
  input  A1,
  input  B1,
  input  A0,
  input  B0,
  input  C_in,
  output S4,
  output S3,
  output S2,
  output S1,
  output S0
);

  wire [1:0] generate_1_out_3, generate_3_out_3, generate_4_out_3, generate_5_out_3, half_adder_1_out_3,
       half_adder_2_out_3, half_adder_3_out_3, half_adder_4_out_3;
  wire [1:1] generate_2_out_3;

  half_adder half_adder_1 (.in_1(A3), .in_2(B3), .out_3(half_adder_1_out_3));
  \generate  generate_1 (.in_1(half_adder_1_out_3), .in_2(half_adder_2_out_3), .out_3(generate_1_out_3));
  \generate  generate_2 (.in_1(generate_1_out_3), .in_2(generate_5_out_3), .out_3({generate_2_out_3[1], S4}));
  half_adder half_adder_2 (.in_1(A2), .in_2(B2), .out_3(half_adder_2_out_3));
  \generate  generate_3 (.in_1(half_adder_2_out_3), .in_2(half_adder_4_out_3), .out_3(generate_3_out_3));
  \generate  generate_4 (.in_1(generate_3_out_3), .in_2(half_adder_3_out_3), .out_3(generate_4_out_3));
  xor xor_1 (S2, half_adder_2_out_3[1], generate_5_out_3[0]);
  xor xor_2 (S3, half_adder_1_out_3[1], generate_4_out_3[0]);
  half_adder half_adder_3 (.in_1(A0), .in_2(B0), .out_3(half_adder_3_out_3));
  half_adder half_adder_4 (.in_1(A1), .in_2(B1), .out_3(half_adder_4_out_3));
  \generate  generate_5 (.in_1(half_adder_4_out_3), .in_2(half_adder_3_out_3), .out_3(generate_5_out_3));
  xor xor_3 (S1, half_adder_4_out_3[1], half_adder_3_out_3[0]);
  xor xor_4 (S0, half_adder_3_out_3[1], C_in);

  // Notes on the sheet:
  //   Input
  //   Output
  //   Half Adders
  //   Carry Lookahead
  //   Half Adders
endmodule

module half_adder (
  input  in_1,
  input  in_2,
  output [1:0] out_3
);

  xor xor_1 (out_3[1], in_1, in_2);
  and and_1 (out_3[0], in_1, in_2);
endmodule

module \generate  (
  input  [1:0] in_1,
  input  [1:0] in_2,
  output [1:0] out_3
);

  wire and_2_out;

  and and_1 (out_3[1], in_1[1], in_2[1]);
  and and_2 (and_2_out, in_1[1], in_2[0]);
  or or_1 (out_3[0], in_1[0], and_2_out);
endmodule
