// Logisim project multi-circuit.circ as structural Verilog: 1 circuit, main circuit main
module main (
  input  [7:0] in_1,
  input  [7:0] in_2,
  input  [2:0] in_3,
  output [7:0] out_4
);

  wire [2:0] rom_1_data;
  wire [7:0] controlled_buffer_1_out, or_1_out, pull_resistor_2_node, xor_1_out, xor_2_out, xor_3_out,
       xor_4_out, xor_5_out;

  assign controlled_buffer_1_out = rom_1_data[2] ? {8{1'b1}} : 8'bz;  // Controlled_Buffer controlled_buffer_1
  Pull_Resistor pull_resistor_1 (.node(controlled_buffer_1_out));
  assign xor_1_out = in_1 ^ in_2;  // XOR_Gate xor_1, 8 bits wide
  assign xor_2_out = controlled_buffer_1_out ^ in_1;  // XOR_Gate xor_2, 8 bits wide
  assign xor_3_out = in_2 ^ controlled_buffer_1_out;  // XOR_Gate xor_3, 8 bits wide
  ROM #(.addrWidth(3), .dataWidth(3)) rom_1 (.addr(in_3), .data(rom_1_data));  // open: sel
  assign or_1_out = xor_2_out | xor_3_out;  // OR_Gate or_1, 8 bits wide
  Pull_Resistor pull_resistor_2 (.node(pull_resistor_2_node));
  assign pull_resistor_2_node = rom_1_data[1] ? {8{1'b1}} : 8'bz;  // Controlled_Buffer controlled_buffer_2
  assign xor_4_out = xor_1_out ^ pull_resistor_2_node;  // XOR_Gate xor_4, 8 bits wide
  assign xor_5_out = or_1_out ^ pull_resistor_2_node;  // XOR_Gate xor_5, 8 bits wide
  Multiplexer #(.width(8)) multiplexer_1 (
    .in0(xor_4_out), .in1(xor_5_out), .out(out_4), .sel(rom_1_data[0]));  // open: en

  // Notes on the sheet:
  //   contents of rom_1 (hex, n*v repeats v):
  //   1
endmodule
