// Logisim project my ALU 2.circ as structural Verilog: 2 circuits, main circuit main
module main (
  input  [7:0] in_1,
  input  [7:0] in_2,
  input  [3:0] in_3,
  output [7:0] out_4
);

  wire adder_1_cout, multiplexer_1_out, subtractor_1_bout, undriven, undriven_2;
  wire [7:0] adder_1_out, and_1_out, divider_1_out, divider_1_rem, multiplier_1_cout, multiplier_1_out,
       nand_1_out, nor_1_out, not_1_out, or_1_out, subtractor_1_out, xnor_1_out, xor_1_out;

  Subtractor subtractor_1 (.a(in_1), .b(in_2), .out(subtractor_1_out), .bout(subtractor_1_bout));  // open: bin
  Adder adder_1 (.a(in_1), .b(in_2), .out(adder_1_out), .cout(adder_1_cout));  // open: cin
  assign not_1_out = ~in_1;  // NOT_Gate not_1, 8 bits wide
  assign and_1_out = in_1 & in_2;  // AND_Gate and_1, 8 bits wide
  assign or_1_out = in_1 | in_2;  // OR_Gate or_1, 8 bits wide
  assign nand_1_out = ~(in_1 & in_2);  // NAND_Gate nand_1, 8 bits wide
  assign nor_1_out = ~(in_1 | in_2);  // NOR_Gate nor_1, 8 bits wide
  assign xor_1_out = in_1 ^ in_2;  // XOR_Gate xor_1, 8 bits wide
  assign xnor_1_out = ~(in_1 ^ in_2);  // XNOR_Gate xnor_1, 8 bits wide
  Multiplier multiplier_1 (.a(in_1), .b(in_2), .out(multiplier_1_out), .cout(multiplier_1_cout));  // open: cin
  mult_div_carry mult_div_carry_1 (.in_1(multiplier_1_cout), .in_2(divider_1_rem), .in_3(undriven_2), .in_4(undriven));
  Multiplexer #(.select(4)) multiplexer_1 (
    .in6(adder_1_cout), .in7(subtractor_1_bout), .in8(undriven_2), .in9(undriven), .out(multiplexer_1_out),
    .sel(in_3));  // open: in0, in1, in2, in3, in4, in5, in10, in11, in12, in13, in14, in15, en
  Divider divider_1 (.a(in_1), .b(in_2), .out(divider_1_out), .rem(divider_1_rem));  // open: upper
  Multiplexer #(.select(4), .width(8)) multiplexer_2 (
    .in0(and_1_out), .in1(or_1_out), .in2(nand_1_out), .in3(nor_1_out), .in4(xor_1_out), .in5(xnor_1_out),
    .in6(adder_1_out), .in7(subtractor_1_out), .in8(multiplier_1_out), .in9(divider_1_out), .in10(not_1_out),
    .out(out_4), .sel(in_3));  // open: in11, in12, in13, in14, in15, en
  Pull_Resistor pull_resistor_1 (.node(multiplexer_1_out));
  LED led_1 (.in(multiplexer_1_out));

  // Notes on the sheet:
  //   A
  //   B
  //   wiring must match  main mux
endmodule

module mult_div_carry (
  input  [7:0] in_1,
  input  [7:0] in_2,
  input  in_3,
  input  in_4
);

  or or_1 (in_3, in_1[7], in_1[6], in_1[5], in_1[4], in_1[3], in_1[2], in_1[1], in_1[0]);
  or or_2 (in_4, in_2[7], in_2[6], in_2[5], in_2[4], in_2[3], in_2[2], in_2[1], in_2[0]);
endmodule
