// Logisim project number display.circ as structural Verilog: 1 circuit, main circuit main
module main (
  input  in_1,
  input  in_2,
  input  in_3,
  input  in_4,
  input  in_5,
  input  in_6,
  input  in_7,
  input  in_8,
  input  in_9,
  input  in_10,
  input  in_11
);

  wire [3:0] priority_encoder_1_out;
  wire [14:0] rom_1_data;

  Priority_Encoder #(.select(4), .disabled(0)) priority_encoder_1 (
    .in0(in_1), .in1(in_2), .in2(in_3), .in3(in_4), .in4(in_5), .in5(in_6), .in6(in_7), .in7(in_8),
    .in8(in_9), .in9(in_10), .out(priority_encoder_1_out), .en_in(in_11));  // open: in10, in11, in12, in13, in14, in15, gs, en_out
  ROM #(.addrWidth(4), .dataWidth(15)) rom_1 (.addr(priority_encoder_1_out), .data(rom_1_data));  // open: sel
  DotMatrix #(.inputtype("row"), .matrixcols(3), .matrixrows(5)) dotmatrix_1 (
    .row0(rom_1_data[14:12]), .row1(rom_1_data[11:9]), .row2(rom_1_data[8:6]), .row3(rom_1_data[5:3]),
    .row4(rom_1_data[2:0]));

  // Notes on the sheet:
  //   contents of rom_1 (hex, n*v repeats v):
  //   2b6a 2c97 62a7 638e 4*0 7fff 0 7fda
  //   Used binary to hex converter
endmodule
