// Logisim project order lock.circ as structural Verilog: 1 circuit, main circuit main
module main (
  input  [1:0] in_1,
  input  _1,
  input  _2,
  input  _3
);

  wire and_2_out, button_1_out, button_2_out, not_1_out;
  wire [3:0] and_1_out, shift_register_1_q3, shift_register_2_q3, shift_register_3_q3, xnor_1_out,
       xnor_2_out, xnor_3_out;
  wire [11:0] rom_1_data;

  Shift_Register #(.length(4)) shift_register_1 (
    .in(_1), .clk(button_1_out), .clr(button_2_out), .q0(shift_register_1_q3[3]),
    .q1(shift_register_1_q3[2]), .q2(shift_register_1_q3[1]), .q3(shift_register_1_q3[0]));  // open: shift, out, load, d0, d1, d2, d3
  Shift_Register #(.length(4)) shift_register_2 (
    .in(_2), .clk(button_1_out), .clr(button_2_out), .q0(shift_register_2_q3[3]),
    .q1(shift_register_2_q3[2]), .q2(shift_register_2_q3[1]), .q3(shift_register_2_q3[0]));  // open: shift, out, load, d0, d1, d2, d3
  Shift_Register #(.length(4)) shift_register_3 (
    .in(_3), .clk(button_1_out), .clr(button_2_out), .q0(shift_register_3_q3[3]),
    .q1(shift_register_3_q3[2]), .q2(shift_register_3_q3[1]), .q3(shift_register_3_q3[0]));  // open: shift, out, load, d0, d1, d2, d3
  Button button_1 (.out(button_1_out));
  Button button_2 (.out(button_2_out));
  ROM #(.addrWidth(2), .dataWidth(12)) rom_1 (.addr(in_1), .data(rom_1_data));  // open: sel
  assign xnor_1_out = ~(rom_1_data[11:8] ^ shift_register_1_q3);  // XNOR_Gate xnor_1, 4 bits wide
  assign xnor_2_out = ~(shift_register_2_q3 ^ rom_1_data[7:4]);  // XNOR_Gate xnor_2, 4 bits wide
  assign xnor_3_out = ~(rom_1_data[3:0] ^ shift_register_3_q3);  // XNOR_Gate xnor_3, 4 bits wide
  assign and_1_out = xnor_1_out & xnor_2_out & xnor_3_out;  // AND_Gate and_1, 4 bits wide
  and and_2 (and_2_out, and_1_out[0], and_1_out[1], and_1_out[2], and_1_out[3]);
  LED led_1 (.in(not_1_out));
  not not_1 (not_1_out, and_2_out);
  LED led_2 (.in(and_2_out));

  // Notes on the sheet:
  //   Next key
  //   Clear
  //   Code: 2312
  //   contents of rom_1 (hex, n*v repeats v):
  //   492
endmodule
