// Logisim project real encyrption.circ as structural Verilog: 2 circuits, main circuit main
module main (
  input  [7:0] Input,
  input  [7:0] Key,
  output [7:0] Output
);

  wire [7:0] round_1_out_3, round_2_out_3, round_3_out_3;

  round round_1 (.in_1(Input), .out_3(round_1_out_3), .in_2(Key));
  round round_2 (.in_1(round_1_out_3), .out_3(round_2_out_3), .in_2(Key));
  round round_3 (.in_1(round_2_out_3), .out_3(round_3_out_3), .in_2(Key));
  round round_4 (.in_1(round_3_out_3), .out_3(Output), .in_2(Key));
endmodule

module round (
  input  [7:0] in_1,
  input  [7:0] in_2,
  output [7:0] out_3
);

  wire [7:0] xor_1_out;

  assign xor_1_out = in_1 ^ in_2;  // XOR_Gate xor_1, 8 bits wide
  Shifter #(.shift("rl")) shifter_1 (.in(xor_1_out), .\dist (3'b001), .out(out_3));
endmodule
