// Logisim project rock paper scissors.circ as structural Verilog
module main (
);

  wire button_1_out, button_2_out, button_3_out, button_4_out, button_5_out, button_6_out, button_7_out;
  wire [2:0] logic_out_10, logic_out_11;

  Button button_1 (.out(button_1_out));
  Button button_2 (.out(button_2_out));
  Button button_3 (.out(button_3_out));
  Button button_4 (.out(button_4_out));
  \logic  \logic  (
    .Reset(button_1_out), .in_2(button_4_out), .in_3(button_3_out), .in_4(button_2_out),
    .out_10(logic_out_10), .out_11(logic_out_11), .in_5(button_5_out), .in_6(button_6_out),
    .in_7(button_7_out));  // open: out_8, out_9
  DotMatrix #(.matrixcols(1), .matrixrows(3)) dotmatrix_1 (.col0(logic_out_10));
  DotMatrix #(.matrixcols(1), .matrixrows(3)) dotmatrix_2 (.col0(logic_out_11));
  Button button_5 (.out(button_5_out));
  Button button_6 (.out(button_6_out));
  Button button_7 (.out(button_7_out));

  // Notes on the sheet:
  //   Reset
  //   Rock
  //   Paper
  //   Scissors
endmodule

module \logic  (
  input  Reset,
  input  in_2,
  input  in_3,
  input  in_4,
  input  in_5,
  input  in_6,
  input  in_7,
  output [2:0] out_8,
  output [2:0] out_9,
  output [2:0] out_10,
  output [2:0] out_11
);

  wire and_1_out, or_1_out, or_2_out;

  S_R_Flip_Flop s_r_ff_1 (.Q(out_8[1]), .preset(in_3), .reset(Reset));  // open: S, clk, R, Qn, en
  S_R_Flip_Flop s_r_ff_2 (.Q(out_8[0]), .preset(in_2), .reset(Reset));  // open: S, clk, R, Qn, en
  or or_1 (or_1_out, out_8[0], out_8[1], out_8[2]);
  S_R_Flip_Flop s_r_ff_3 (.Q(out_8[2]), .preset(in_4), .reset(Reset));  // open: S, clk, R, Qn, en
  Pull_Resistor pull_resistor_1 (.node(out_10));
  assign out_10 = and_1_out ? out_8 : 3'bz;  // Controlled_Buffer controlled_buffer_1
  Pull_Resistor pull_resistor_2 (.node(out_11));
  and and_1 (and_1_out, or_1_out, or_2_out);
  assign out_11 = and_1_out ? out_9 : 3'bz;  // Controlled_Buffer controlled_buffer_2
  S_R_Flip_Flop s_r_ff_4 (.Q(out_9[2]), .preset(in_5), .reset(Reset));  // open: S, clk, R, Qn, en
  S_R_Flip_Flop s_r_ff_5 (.Q(out_9[1]), .preset(in_6), .reset(Reset));  // open: S, clk, R, Qn, en
  or or_2 (or_2_out, out_9[2], out_9[0], out_9[1]);
  S_R_Flip_Flop s_r_ff_6 (.Q(out_9[0]), .preset(in_7), .reset(Reset));  // open: S, clk, R, Qn, en

  // Notes on the sheet:
  //   spr
  //   Display Output
  //   rps
  //   2P/1P
endmodule
