// Logisim project rule 110.circ as structural Verilog: 2 circuits, main circuit main
module main (
  input  in_1
);

  wire rule_unit_1_display, rule_unit_2_display, rule_unit_2_x, rule_unit_3_display, rule_unit_4_display,
       rule_unit_4_x, rule_unit_5_display, rule_unit_5_x, rule_unit_6_display, rule_unit_7_display,
       rule_unit_7_x, rule_unit_8_display, rule_unit_8_x, rule_unit_9_display, rule_unit_9_x,
       rule_unit_10_display, rule_unit_11_display, rule_unit_11_x, rule_unit_12_display,
       rule_unit_13_display, rule_unit_14_display, rule_unit_14_x, rule_unit_15_display;

  LED led_1 (.in(rule_unit_1_display));
  Rule_Unit rule_unit_1 (.a(1'b0), .b(1'b0), .c(rule_unit_2_x), .Display(rule_unit_1_display));  // open: x
  Rule_Unit rule_unit_2 (.a(1'b0), .b(1'b0), .c(rule_unit_4_x), .x(rule_unit_2_x), .Display(rule_unit_2_display));
  LED led_2 (.in(rule_unit_2_display));
  LED led_3 (.in(rule_unit_3_display));
  Rule_Unit rule_unit_3 (.a(1'b0), .b(rule_unit_2_x), .c(rule_unit_5_x), .Display(rule_unit_3_display));  // open: x
  Rule_Unit rule_unit_4 (.a(1'b0), .b(1'b0), .c(rule_unit_7_x), .x(rule_unit_4_x), .Display(rule_unit_4_display));
  LED led_4 (.in(rule_unit_4_display));
  Rule_Unit rule_unit_5 (
    .a(1'b0), .b(rule_unit_4_x), .c(rule_unit_8_x), .x(rule_unit_5_x), .Display(rule_unit_5_display));
  LED led_5 (.in(rule_unit_5_display));
  LED led_6 (.in(rule_unit_6_display));
  Rule_Unit rule_unit_6 (
    .a(rule_unit_2_x), .b(rule_unit_5_x), .c(rule_unit_9_x), .Display(rule_unit_6_display));  // open: x
  Rule_Unit rule_unit_7 (.a(1'b0), .b(1'b0), .c(rule_unit_11_x), .x(rule_unit_7_x), .Display(rule_unit_7_display));
  LED led_7 (.in(rule_unit_7_display));
  Rule_Unit rule_unit_8 (
    .a(1'b0), .b(rule_unit_7_x), .c(rule_unit_7_x), .x(rule_unit_8_x), .Display(rule_unit_8_display));
  LED led_8 (.in(rule_unit_8_display));
  Rule_Unit rule_unit_9 (
    .a(rule_unit_4_x), .b(rule_unit_8_x), .c(rule_unit_8_x), .x(rule_unit_9_x), .Display(rule_unit_9_display));
  LED led_9 (.in(rule_unit_9_display));
  LED led_10 (.in(rule_unit_10_display));
  Rule_Unit rule_unit_10 (
    .a(rule_unit_5_x), .b(rule_unit_9_x), .c(rule_unit_14_x), .Display(rule_unit_10_display));  // open: x
  LED led_11 (.in(rule_unit_11_display));
  Rule_Unit rule_unit_11 (.a(1'b0), .b(in_1), .c(1'b0), .x(rule_unit_11_x), .Display(rule_unit_11_display));
  LED led_12 (.in(rule_unit_12_display));
  Rule_Unit rule_unit_12 (.a(1'b0), .b(rule_unit_11_x), .c(1'b0), .x(rule_unit_7_x), .Display(rule_unit_12_display));
  LED led_13 (.in(rule_unit_13_display));
  Rule_Unit rule_unit_13 (
    .a(rule_unit_7_x), .b(rule_unit_7_x), .c(1'b0), .x(rule_unit_8_x), .Display(rule_unit_13_display));
  LED led_14 (.in(rule_unit_14_display));
  Rule_Unit rule_unit_14 (
    .a(rule_unit_8_x), .b(rule_unit_8_x), .c(1'b0), .x(rule_unit_14_x), .Display(rule_unit_14_display));
  Rule_Unit rule_unit_15 (.a(rule_unit_9_x), .b(rule_unit_14_x), .c(1'b0), .Display(rule_unit_15_display));  // open: x
  LED led_15 (.in(rule_unit_15_display));
endmodule

module Rule_Unit (
  input  a,
  input  b,
  input  c,
  output Display,
  output x
);

  wire and_1_out, and_2_out, and_3_out, not_1_out, not_2_out, not_3_out;

  not not_1 (not_1_out, b);
  not not_2 (not_2_out, a);
  not not_3 (not_3_out, c);
  and and_1 (and_1_out, not_1_out, c);
  and and_2 (and_2_out, not_2_out, b);
  and and_3 (and_3_out, b, not_3_out);
  or or_1 (Display, and_1_out, and_2_out, and_3_out);

  assign x = Display;
endmodule
