// Logisim project scrolling display.circ as structural Verilog: 1 circuit, main circuit main
module main (
  input  in_1
);

  wire clock_1_out;
  wire [4:0] counter_1_q, ram_1_data, shift_register_1_q0, shift_register_1_q1, shift_register_1_q2,
       shift_register_1_q3, shift_register_1_q4, shift_register_1_q5, shift_register_1_q6,
       shift_register_1_q7;

  Counter #(.width(5), .max('h1f)) counter_1 (.Q(counter_1_q), .clk(clock_1_out));  // open: load, D, count, carry, clr
  Clock clock_1 (.out(clock_1_out));
  RAM #(.addrWidth(5), .dataWidth(5)) ram_1 (.addr(counter_1_q), .data(ram_1_data));  // open: sel, clk, ld, clr
  Shift_Register #(.width(5)) shift_register_1 (
    .in(ram_1_data), .clk(clock_1_out), .clr(in_1), .q0(shift_register_1_q0), .q1(shift_register_1_q1),
    .q2(shift_register_1_q2), .q3(shift_register_1_q3), .q4(shift_register_1_q4), .q5(shift_register_1_q5),
    .q6(shift_register_1_q6), .q7(shift_register_1_q7));  // open: shift, out, load, d0, d1, d2, d3, d4, d5, d6, d7
  DotMatrix #(.matrixcols(8), .matrixrows(5)) dotmatrix_1 (
    .col0(shift_register_1_q7), .col1(shift_register_1_q6), .col2(shift_register_1_q5),
    .col3(shift_register_1_q4), .col4(shift_register_1_q3), .col5(shift_register_1_q2),
    .col6(shift_register_1_q1), .col7(shift_register_1_q0));
endmodule
